// Digital circuit sample1.dig as structural Verilog
module sample1 (
  input  [1:0] A1,
  input  [1:0] A2,
  input  [1:0] A3,
  output [1:0] Y1
);

  assign Y1 = A1 & ~A3 & A2;  // And and_1, 2 bits wide
  // Probe on A3
endmodule
