// Digital circuit segment.dig as structural Verilog
module segment (
  input  D_3,
  input  D_2,
  input  D_1,
  input  D_0
);

  wire synthesise_1_a, synthesise_1_b, synthesise_1_c, synthesise_1_d, synthesise_1_dp, synthesise_1_e,
       synthesise_1_f, synthesise_1_g;

  Synthesise synthesise_1 (
    .A_2(D_3), .B_2(D_2), .C_2(D_1), .D_2(D_0), .dp(synthesise_1_dp), .a(synthesise_1_a), .b(synthesise_1_b),
    .c(synthesise_1_c), .d(synthesise_1_d), .e(synthesise_1_e), .f(synthesise_1_f), .g(synthesise_1_g));
  Seven_Seg seven_seg_1 (
    .a(synthesise_1_a), .b(synthesise_1_b), .c(synthesise_1_c), .d(synthesise_1_d), .e(synthesise_1_e),
    .f(synthesise_1_f), .g(synthesise_1_g), .dp(synthesise_1_dp));
endmodule
