// Digital circuit hard logic-III.dig as structural Verilog
module hard_logic_III (
  input  [7:0] IN,
  input  clock,
  input  hand,
  input  model,
  input  reset,
  output [7:0] OUT
);

  wire and_1_out, and_2_out, and_5_out, and_8_out, break_q, C, C_F, clk, ENout, hlt, I_0, I_10, LDPC, M1, M2,
       memw, multiplexer_1_out, multiplexer_3_out, nand_1_out, NOP, P2, PC_INC, PC_plus_1, regw, S, S_F, Z,
       Z_F;
  wire [1:0] Asel, Ra, Rb;
  wire [2:0] ALUop, bitextender_1_out, Ssel;
  wire [3:0] counter_1_out, OP;
  wire [6:0] multiplexer_7_out;
  wire [7:0] add_1_s, add_2_s, and_9_out, barrelshifter_1_out, barrelshifter_2_out, barrelshifter_3_out,
       barrelshifter_4_out, bitextender_2_out, Da, Db, Dram_d, Drom_d, Min, Mout, mul_1_mul,
       multiplexer_2_out, multiplexer_8_out, or_3_out, out_t, PC_q, register_1_q, Rin, sub_1_s, Xin,
       xor_1_out, Yin;
  wire [7:1] IMM;
  wire [15:8] mul_1_mul_2;

  Multiplexer #(.Selector_Bits(2)) multiplexer_1 (
    .sel(Rb), .in_0(1'b1), .in_1(C), .in_2(Z), .in_3(S), .out(multiplexer_1_out));
  and and_1 (and_1_out, multiplexer_1_out, LDPC);
  Register #(.Bits(3)) ALU_Flag (.D({S_F, Z_F, C_F}), .C(M1), .en(1'b1), .Q({S, Z, C}));
  // Probe on {IMM, I_0}
  Multiplexer #(.Bits(8)) multiplexer_2 (.sel(and_1_out), .in_0(add_1_s), .in_1({IMM, I_0}), .out(multiplexer_2_out));
  // Probe on multiplexer_2_out
  Register #(.Bits(8)) PC (.D(multiplexer_2_out), .C(clk), .en(PC_plus_1), .Q(PC_q));
  and and_2 (and_2_out, ~NOP, M1);  // And
  D_FF M (.D(and_2_out), .C(clk), .Q(M2), .nQ(M1));
  LED u_M1 (.in(M1));
  LED u_M2 (.in(M2));
  Add #(.Bits(8)) add_1 (.a(8'h1), .b(PC_q), .c_i(1'b0), .s(add_1_s));  // open: c_o
  Multiplexer multiplexer_3 (.sel(model), .in_0(hand), .in_1(clock), .out(multiplexer_3_out));
  // Probe on PC_q
  or or_1 (clk, multiplexer_3_out, break_q);
  ROM #(.AddrBits(8), .Bits(8)) ROM (.A(PC_q), .sel(1'b1), .D({IMM, I_0}));
  BitExtender #(.inputBits(1), .outputBits(3)) bitextender_1 (.in(OP[3]), .out(bitextender_1_out));
  // logic_III logic_iii_1: pin names not known; wires that end beside it: OP, LDPC, PC_INC, P2, Ssel, Asel
  and and_3 (hlt, I_0, NOP, M1);
  BitExtender #(.inputBits(1), .outputBits(8)) bitextender_2 (.in(M2), .out(bitextender_2_out));
  assign ALUop = OP[2:0] & bitextender_1_out;  // And and_4, 3 bits wide
  and and_5 (and_5_out, reset, multiplexer_3_out);
  nor nor_1 (NOP, IMM[4], IMM[5], IMM[6], IMM[7]);
  Register #(.Bits(8)) register_1 (.D({IMM, I_0}), .C(clk), .en(M1), .Q(register_1_q));
  assign {OP, Ra, Rb} = register_1_q & bitextender_2_out;  // And and_6, 8 bits wide
  Seven_Seg_Hex seven_seg_hex_1 (.d(counter_1_out), .dp(1'b0));
  Counter #(.Bits(4)) counter_1 (.en(1'b1), .C(M1), .clr(1'b0), .out(counter_1_out));  // open: ovf
  D_FF_AS \break  (.Set(1'b0), .D(hlt), .C(clk), .Clr(and_5_out), .Q(break_q));  // open: nQ
  // Probe on {OP, Ra, Rb}
  LED led_1 (.in(break_q));
  nand nand_1 (nand_1_out, I_10, P2);
  and and_7 (PC_plus_1, nand_1_out, PC_INC);
  or or_2 (I_10, Rb[0], Rb[1]);
  Multiplexer #(.Bits(8)) multiplexer_4 (.sel(I_10), .in_0({IMM, I_0}), .in_1(Db), .out(Yin));
  and and_8 (and_8_out, memw, ~Yin[7]);  // And
  // Probe on Min
  RAMDualPort #(.AddrBits(7), .Bits(8)) Dram (.A(Yin[6:0]), .Din(Min), .str(and_8_out), .C(clk), .ld(1'b1), .D(Dram_d));
  ROM #(.AddrBits(7), .Bits(8)) Drom (.A(Yin[6:0]), .sel(1'b1), .D(Drom_d));
  Register #(.Bits(8)) register_2 (.D(out_t), .C(clk), .en(ENout), .Q(OUT));
  // Probe on Rin
  RegisterFile #(.Bits(8)) regs (.Din(Rin), .we(regw), .Rw(Ra), .C(clk), .Ra(Ra), .Rb(Rb), .Da(Da), .Db(Db));
  Multiplexer #(.Bits(8)) multiplexer_5 (.sel(Yin[7]), .in_0(Dram_d), .in_1(Drom_d), .out(Mout));
  // Probe on Da
  // Probe on Db
  // Probe on Mout
  LED led_2 (.in(OUT[7]));
  // Probe on Yin
  Add #(.Bits(8)) add_2 (.a(Xin), .b(Yin), .c_i(1'b0), .s(add_2_s), .c_o(C_F));
  Sub #(.Bits(8)) sub_1 (.a(Xin), .b(Yin), .c_i(1'b0), .s(sub_1_s));  // open: c_o
  Mul #(.Bits(8)) mul_1 (.a(Xin), .b(Yin), .mul({mul_1_mul_2, mul_1_mul}));
  assign and_9_out = Xin & Yin;  // And and_9, 8 bits wide
  assign or_3_out = Xin | Yin;  // Or or_3, 8 bits wide
  assign xor_1_out = Xin ^ Yin;  // XOr xor_1, 8 bits wide
  // Probe on Ssel
  Multiplexer #(.Selector_Bits(3), .Bits(8)) multiplexer_6 (
    .sel(Ssel), .in_0({8{1'b0}}), .in_1(Da), .in_2(Mout), .in_3(IN), .in_4({IMM, I_0}), .in_5(Db),
    .in_6({8{1'b0}}), .in_7({8{1'b0}}), .out(Xin));
  // Probe on Xin
  // Probe on ALUop
  Multiplexer #(.Selector_Bits(3), .Bits(8)) multiplexer_7 (
    .sel(ALUop), .in_0(Xin), .in_1(add_2_s), .in_2(sub_1_s), .in_3(mul_1_mul), .in_4(and_9_out),
    .in_5(or_3_out), .in_6(xor_1_out), .in_7(multiplexer_8_out), .out({S_F, multiplexer_7_out}));
  BarrelShifter #(.Bits(8)) barrelshifter_1 (.in(Xin), .shift({IMM[3:1], I_0}), .out(barrelshifter_1_out));
  BarrelShifter #(.Bits(8), .direction("right")) barrelshifter_2 (
    .in(Xin), .shift({IMM[3:1], I_0}), .out(barrelshifter_2_out));
  BarrelShifter #(.Bits(8), .barrelShifterMode("rotate")) barrelshifter_3 (
    .in(Xin), .shift({IMM[3:1], I_0}), .out(barrelshifter_3_out));
  BarrelShifter #(.Bits(8), .barrelShifterMode("rotate"), .direction("right")) barrelshifter_4 (
    .in(Xin), .shift({IMM[3:1], I_0}), .out(barrelshifter_4_out));
  // Probe on {IMM[3:1], I_0}
  Comparator #(.Bits(8)) comparator_1 (.a({S_F, multiplexer_7_out}), .b({8{1'b0}}), .eq(Z_F));  // open: gt, lt
  Decoder #(.Selector_Bits(2)) decoder_1 (.sel(Asel), .out_1(regw), .out_2(memw), .out_3(ENout));  // open: out_0
  // Probe on Asel
  Demultiplexer #(.Selector_Bits(2), .Bits(8)) demultiplexer_1 (
    .sel(Asel), .in({S_F, multiplexer_7_out}), .out_1(Rin), .out_2(Min), .out_3(out_t));  // open: out_0
  Multiplexer #(.Selector_Bits(2), .Bits(8)) multiplexer_8 (
    .sel(Rb), .in_0(barrelshifter_1_out), .in_1(barrelshifter_2_out), .in_2(barrelshifter_3_out),
    .in_3(barrelshifter_4_out), .out(multiplexer_8_out));
  // Probe on Rb

  // Other names for the same wires on the sheet: IMM[0] = I_0

  // Notes on the sheet:
  //   clock: Hz: 2
  //   硬布线控制器
  //   contents of ROM (hex, n*v repeats v):
  //   30,1,34,2,38,80,1,91,94,1,f9,1,12,10,10,7,50,1
  //   存储器
  //   寄存器
  //   contents of Drom (hex, n*v repeats v):
  //   0,fffff0b7,400093,40016f,158513,feb50fe3,fff20193,318233,308023,309023,30a023,40a223,
  //   402383,800403,801403,804403,805403,802403,ff3a413,ffe3b413,fff44413,247493,249513,
  //   1f4d593,25d593,40125613,40460633,c616b3,c42733,c43733,864733,e6d7b3,40f75733,d77733,
  //   c76833,200713,11d873,11d873,810f3,710f3,a973,25973,1039f3,10f9f3,e7
  //   数据通路+运算器
endmodule
