// Digital circuit microprogram-int.dig as structural Verilog
module microprogram_int (
  input  [7:0] IN,
  input  clock,
  input  hand,
  input  model,
  input  reset,
  input  [7:0] ISR,
  output [7:0] OUT
);

  wire and_2_out, and_5_out, and_7_out, break_q, C, C_F, clk, d_ff_1_q, d_ff_2_q, d_ff_as_1_q, ENout, hlt,
       I_0, I_1, I_10, \int , key_out, LDPC, memw, multiplexer_1_out, multiplexer_7_out, nand_1_out,
       nor_1_out, P1, P2, PC_INC, PC_plus_1, register_1_q, regw, ret, S, S_F, Z, Z_F;
  wire [1:0] Asel, Ra, Rb;
  wire [2:0] ALUop, Flag, multiplexer_2_out, Ssel;
  wire [3:0] counter_1_out, MAR_q, MROM_d, multiplexer_5_out;
  wire [6:0] multiplexer_11_out;
  wire [7:0] add_1_s, add_2_s, and_8_out, barrelshifter_1_out, barrelshifter_2_out, barrelshifter_3_out,
       barrelshifter_4_out, Da, Db, Dram_d, Drom_d, mepc, Min, Mout, mul_1_mul, multiplexer_3_out,
       multiplexer_4_out, multiplexer_6_out, multiplexer_12_out, or_3_out, out_t, PC_int, Rin, sub_1_s, Xin,
       xor_1_out, Yin;
  wire [7:2] IMM;
  wire [15:8] mul_1_mul_2;

  Register register_1 (.D(ret), .C(clk), .en(P1), .Q(register_1_q));
  Button key (.out(key_out));
  Multiplexer #(.Selector_Bits(2)) multiplexer_1 (
    .sel(Rb), .in_0(1'b1), .in_1(C), .in_2(Z), .in_3(S), .out(multiplexer_1_out));
  Multiplexer #(.Bits(3)) multiplexer_2 (
    .sel(register_1_q), .in_0({S_F, Z_F, C_F}), .in_1(Flag), .out(multiplexer_2_out));
  D_FF_AS d_ff_as_1 (.Set(1'b0), .D(1'b1), .C(key_out), .Clr(d_ff_1_q), .Q(d_ff_as_1_q));  // open: nQ
  Register #(.Bits(3)) BP_Flag (.D({S, Z, C}), .C(clk), .en(\int ), .Q(Flag));
  // Probe on multiplexer_2_out
  Register #(.Bits(3)) ALU_Flag (.D(multiplexer_2_out), .C(P1), .en(1'b1), .Q({S, Z, C}));
  // Probe on PC_int
  Register #(.Bits(8)) BP_pc (.D(PC_int), .C(clk), .en(\int ), .Q(mepc));
  D_FF d_ff_1 (.D(d_ff_2_q), .C(clk), .Q(d_ff_1_q));  // open: nQ
  D_FF d_ff_2 (.D(d_ff_as_1_q), .C(P1), .Q(d_ff_2_q));  // open: nQ
  and and_1 (\int , d_ff_2_q, P1);
  and and_2 (and_2_out, LDPC, multiplexer_1_out);
  // Probe on Flag
  // Probe on mepc
  Multiplexer #(.Bits(8)) multiplexer_3 (
    .sel(and_2_out), .in_0(add_1_s), .in_1({IMM, I_1, I_0}), .out(multiplexer_3_out));
  Multiplexer #(.Bits(8)) multiplexer_4 (.sel(ret), .in_0(multiplexer_3_out), .in_1(mepc), .out(multiplexer_4_out));
  Register #(.Bits(8)) PC (.D(multiplexer_4_out), .C(clk), .en(PC_plus_1), .Q(PC_int));
  Multiplexer #(.Bits(4)) multiplexer_5 (.sel(P1), .in_0(MROM_d), .in_1(IMM[7:4]), .out(multiplexer_5_out));
  // Probe on multiplexer_4_out
  Multiplexer #(.Bits(8)) multiplexer_6 (.sel(\int ), .in_0(PC_int), .in_1(ISR), .out(multiplexer_6_out));
  // Probe on multiplexer_5_out
  nor nor_1 (nor_1_out, IMM[4], IMM[5], IMM[6]);
  Multiplexer multiplexer_7 (.sel(model), .in_0(hand), .in_1(clock), .out(multiplexer_7_out));
  Register #(.Bits(4)) MAR (.D(multiplexer_5_out), .C(clk), .en(1'b1), .Q(MAR_q));
  and and_3 (hlt, I_0, P1, nor_1_out, ~IMM[7]);  // And
  or or_1 (clk, multiplexer_7_out, break_q);
  Add #(.Bits(8)) add_1 (.a(8'h1), .b(multiplexer_6_out), .c_i(1'b0), .s(add_1_s));  // open: c_o
  // Probe on MAR_q
  ROM #(.AddrBits(4), .Bits(16), .Addr_Bits(6)) MROM (
    .A(MAR_q), .sel(1'b1), .D({ALUop, LDPC, Ssel, PC_INC, Asel, P1, P2, MROM_d}));
  and and_4 (ret, nor_1_out, P1, IMM[7]);
  // Probe on add_1_s
  ROM #(.AddrBits(8), .Bits(8)) ROM (.A(multiplexer_6_out), .sel(1'b1), .D({IMM, I_1, I_0}));
  // Probe on multiplexer_6_out
  // Probe on {ALUop, LDPC, Ssel, PC_INC, Asel, P1, P2, MROM_d}
  and and_5 (and_5_out, reset, multiplexer_7_out);
  // Probe on MROM_d
  // Probe on {IMM, I_1, I_0}
  // Probe on IMM[7:4]
  Register #(.Bits(4)) register_2 (.D({IMM[3:2], I_1, I_0}), .C(clk), .en(P1), .Q({Ra, Rb}));
  Counter #(.Bits(4)) counter_1 (.en(1'b1), .C(P1), .clr(1'b0), .out(counter_1_out));  // open: ovf
  D_FF_AS \break  (.Set(1'b0), .D(hlt), .C(clk), .Clr(and_5_out), .Q(break_q));  // open: nQ
  // Probe on Rb
  // Probe on Ra
  Seven_Seg_Hex seven_seg_hex_1 (.d(counter_1_out), .dp(1'b0));
  LED led_1 (.in(break_q));
  nand nand_1 (nand_1_out, I_10, P2);
  and and_6 (PC_plus_1, nand_1_out, PC_INC);
  or or_2 (I_10, Rb[0], Rb[1]);
  Multiplexer #(.Bits(8)) multiplexer_8 (.sel(I_10), .in_0({IMM, I_1, I_0}), .in_1(Db), .out(Yin));
  and and_7 (and_7_out, memw, ~Yin[7]);  // And
  // Probe on Min
  RAMDualPort #(.AddrBits(7), .Bits(8)) Dram (.A(Yin[6:0]), .Din(Min), .str(and_7_out), .C(clk), .ld(1'b1), .D(Dram_d));
  ROM #(.AddrBits(7), .Bits(8)) Drom (.A(Yin[6:0]), .sel(1'b1), .D(Drom_d));
  Register #(.Bits(8)) register_3 (.D(out_t), .C(clk), .en(ENout), .Q(OUT));
  // Probe on Rin
  RegisterFile #(.Bits(8)) regs (.Din(Rin), .we(regw), .Rw(Ra), .C(clk), .Ra(Ra), .Rb(Rb), .Da(Da), .Db(Db));
  Multiplexer #(.Bits(8)) multiplexer_9 (.sel(Yin[7]), .in_0(Dram_d), .in_1(Drom_d), .out(Mout));
  // Probe on Da
  // Probe on Db
  // Probe on Mout
  LED led_2 (.in(OUT[7]));
  // Probe on Yin
  Add #(.Bits(8)) add_2 (.a(Xin), .b(Yin), .c_i(1'b0), .s(add_2_s), .c_o(C_F));
  Sub #(.Bits(8)) sub_1 (.a(Xin), .b(Yin), .c_i(1'b0), .s(sub_1_s));  // open: c_o
  Mul #(.Bits(8)) mul_1 (.a(Xin), .b(Yin), .mul({mul_1_mul_2, mul_1_mul}));
  assign and_8_out = Xin & Yin;  // And and_8, 8 bits wide
  assign or_3_out = Xin | Yin;  // Or or_3, 8 bits wide
  assign xor_1_out = Xin ^ Yin;  // XOr xor_1, 8 bits wide
  Multiplexer #(.Selector_Bits(3), .Bits(8)) multiplexer_10 (
    .sel(Ssel), .in_0({8{1'b0}}), .in_1(Da), .in_2(Mout), .in_3(IN), .in_4({IMM, I_1, I_0}), .in_5(Db),
    .in_6({8{1'b0}}), .in_7({8{1'b0}}), .out(Xin));
  // Probe on Xin
  // Probe on ALUop
  Multiplexer #(.Selector_Bits(3), .Bits(8)) multiplexer_11 (
    .sel(ALUop), .in_0(Xin), .in_1(add_2_s), .in_2(sub_1_s), .in_3(mul_1_mul), .in_4(and_8_out),
    .in_5(or_3_out), .in_6(xor_1_out), .in_7(multiplexer_12_out), .out({S_F, multiplexer_11_out}));
  BarrelShifter #(.Bits(8)) barrelshifter_1 (.in(Xin), .shift({IMM[3:2], I_1, I_0}), .out(barrelshifter_1_out));
  BarrelShifter #(.Bits(8), .direction("right")) barrelshifter_2 (
    .in(Xin), .shift({IMM[3:2], I_1, I_0}), .out(barrelshifter_2_out));
  BarrelShifter #(.Bits(8), .barrelShifterMode("rotate")) barrelshifter_3 (
    .in(Xin), .shift({IMM[3:2], I_1, I_0}), .out(barrelshifter_3_out));
  BarrelShifter #(.Bits(8), .barrelShifterMode("rotate"), .direction("right")) barrelshifter_4 (
    .in(Xin), .shift({IMM[3:2], I_1, I_0}), .out(barrelshifter_4_out));
  // Probe on {IMM[3:2], I_1, I_0}
  Comparator #(.Bits(8)) comparator_1 (.a({S_F, multiplexer_11_out}), .b({8{1'b0}}), .eq(Z_F));  // open: gt, lt
  Decoder #(.Selector_Bits(2)) decoder_1 (.sel(Asel), .out_1(regw), .out_2(memw), .out_3(ENout));  // open: out_0
  // Probe on Asel
  Demultiplexer #(.Selector_Bits(2), .Bits(8)) demultiplexer_1 (
    .sel(Asel), .in({S_F, multiplexer_11_out}), .out_1(Rin), .out_2(Min), .out_3(out_t));  // open: out_0
  Multiplexer #(.Selector_Bits(2), .Bits(8)) multiplexer_12 (
    .sel(Rb), .in_0(barrelshifter_1_out), .in_1(barrelshifter_2_out), .in_2(barrelshifter_3_out),
    .in_3(barrelshifter_4_out), .out(multiplexer_12_out));

  // Other names for the same wires on the sheet: IMM[1:0] = {I_1, I_0}; OP[3:0] = IMM[7:4]

  // Notes on the sheet:
  //   clock: Hz: 2
  //   微程序控制器
  //   contents of MROM (hex, n*v repeats v):
  //   120,1100,a40,940,640,2c0,550,390,0,2350,4350,6350,8350,a350,c350,e340
  //   contents of ROM (hex, n*v repeats v):
  //   30,1,34,2,38,80,1,91,94,1,f9,1,12,10,10,7,50,1,0,0,0,0,0,0,0,0,0,0,0,0,0,0,50,80
  //   存储器
  //   寄存器
  //   contents of Drom (hex, n*v repeats v):
  //   0,fffff0b7,400093,40016f,158513,feb50fe3,fff20193,318233,308023,309023,30a023,40a223,
  //   402383,800403,801403,804403,805403,802403,ff3a413,ffe3b413,fff44413,247493,249513,
  //   1f4d593,25d593,40125613,40460633,c616b3,c42733,c43733,864733,e6d7b3,40f75733,d77733,
  //   c76833,200713,11d873,11d873,810f3,710f3,a973,25973,1039f3,10f9f3,e7
  //   数据通路+运算器
endmodule
