// Digital circuit Goldschmidt div.dig as structural Verilog
module Goldschmidt_div (
  input  Init,
  input  [15:0] D,
  input  [15:0] X,
  output [15:0] out_2,
  output [15:0] out_3
);

  wire clk_out;
  wire [15:0] d_ff_1_q, d_ff_2_q, div_1_q, div_1_r, multiplexer_1_out, multiplexer_2_out, sub_1_s;
  wire [31:0] mul_1_mul, mul_2_mul;

  D_FF #(.Bits(16)) d_ff_1 (.D(out_3), .C(clk_out), .Q(d_ff_1_q));  // open: nQ
  D_FF #(.Bits(16)) d_ff_2 (.D(mul_2_mul[23:8]), .C(clk_out), .Q(d_ff_2_q));  // open: nQ
  Button clk (.out(clk_out));
  // Probe on d_ff_1_q
  // Probe on d_ff_2_q
  Div #(.Bits(16)) div_1 (.a(X), .b(D), .q(div_1_q), .r(div_1_r));
  Multiplexer #(.Bits(16)) multiplexer_1 (.sel(Init), .in_0(d_ff_1_q), .in_1(X), .out(multiplexer_1_out));
  Multiplexer #(.Bits(16)) multiplexer_2 (.sel(Init), .in_0(d_ff_2_q), .in_1(D), .out(multiplexer_2_out));
  BarrelShifter #(.Bits(16)) barrelshifter_1 (.in(div_1_q), .shift(5'b01000), .out(out_2));
  // Probe on div_1_r
  // Probe on multiplexer_1_out
  Mul #(.Bits(16)) mul_1 (.a(multiplexer_1_out), .b(sub_1_s), .mul({mul_1_mul[31:24], out_3, mul_1_mul[7:0]}));
  Sub #(.Bits(16)) sub_1 (.a(16'h200), .b(multiplexer_2_out), .c_i(1'b0), .s(sub_1_s));  // open: c_o
  Mul #(.Bits(16)) mul_2 (.a(sub_1_s), .b(multiplexer_2_out), .mul(mul_2_mul));
  // Probe on multiplexer_2_out
  // Probe on mul_2_mul[23:8]

  // Notes on the sheet:
  //   D: default 80
  //   X: default 2304
endmodule
