// Digital circuit complex modulus.dig as structural Verilog
module complex_modulus (
  input  [7:0] Q,
  input  [7:0] I,
  output [7:0] R
);

  wire comparator_1_lt, comparator_2_gt;
  wire [7:0] multiplexer_1_out, multiplexer_2_out, multiplexer_3_out, multiplexer_4_out;
  wire [15:0] add_1_s, mul_1_mul, mul_2_mul;

  Comparator #(.Bits(8)) comparator_1 (.a(I), .b(Q), .lt(comparator_1_lt));  // open: gt, eq
  Multiplexer #(.Bits(8)) multiplexer_1 (.sel(comparator_1_lt), .in_0(I), .in_1(Q), .out(multiplexer_1_out));
  Multiplexer #(.Bits(8)) multiplexer_2 (.sel(comparator_1_lt), .in_0(Q), .in_1(I), .out(multiplexer_2_out));
  // Probe Xmax on multiplexer_1_out
  // Probe Ymin on multiplexer_2_out
  Mul #(.Bits(8)) mul_1 (.a(multiplexer_1_out), .b(multiplexer_3_out), .mul(mul_1_mul));
  Mul #(.Bits(8)) mul_2 (.a(multiplexer_4_out), .b(multiplexer_2_out), .mul(mul_2_mul));
  Comparator #(.Bits(8)) comparator_2 (
    .a({multiplexer_2_out[6:0], 1'b0}), .b(multiplexer_1_out), .gt(comparator_2_gt));  // open: eq, lt
  Add #(.Bits(16)) add_1 (
    .a(mul_1_mul), .b(mul_2_mul), .c_i(1'b0), .s({add_1_s[15:14], R, add_1_s[5:0]}));  // open: c_o
  Multiplexer #(.Bits(8)) multiplexer_3 (.sel(comparator_2_gt), .in_0(8'h3f), .in_1(8'h36), .out(multiplexer_3_out));
  Multiplexer #(.Bits(8)) multiplexer_4 (.sel(comparator_2_gt), .in_0(8'hc), .in_1(8'h24), .out(multiplexer_4_out));
  // Probe a on multiplexer_3_out
  // Probe b on multiplexer_4_out

  // Notes on the sheet:
  //   Q: default 64
  //   I: default 48
endmodule
