// Digital circuit ProcessorMux.dig as structural Verilog
// Simple processor based on the MIPS architecture. 
// It is a Harvard single-cycle CPU.
// {{de Einfacher Prozessor, der an die MIPS-Architektur 
// angelehnt ist. Es handelt sich um eine Harvard 
// Single-Cycle CPU.}}
module ProcessorMux (
  input  [15:0] Instr,
  input  Clock,
  input  reset,
  input  [15:0] D_in,
  output [15:0] PC,
  output [15:0] D_out,
  output [15:0] Addr,
  output ioR,
  output ioW
);

  wire abs, ALU2D, alu_1_p6, alu_1_p7, alu_1_p8, ALUop, br, branch_1_p3, branch_1_p4, branch_1_p5, imm, ld,
       muxA, pc_hdl_1_p5, sf, src2D, st, WE;
  wire [1:0] WDmux;
  wire [2:0] muxB;
  wire [15:0] imreg_1_p4, multiplexer_1_out, multiplexer_2_out, multiplexer_3_out, pc_hdl_1_p6,
       ramdualport_1_d, registeropt_1_p6, signext_1_p2, signext_1_p3, signext_1_p4;

  // PC_HDL pc_hdl_1: pin names not known; wires that end beside it: Addr, Clock, abs, reset, pc_hdl_1_p5, pc_hdl_1_p6, PC
  Multiplexer #(.Selector_Bits(2), .Bits(16)) multiplexer_1 (
    .sel(WDmux), .in_0(Addr), .in_1(ramdualport_1_d), .in_2(D_in), .in_3(pc_hdl_1_p6), .out(multiplexer_1_out));
  // ControlMux controlmux_1: pin names not known; wires that end beside it: ioR, ioW, ld, st, br, sf, ALUop, ALU2D, muxA, src2D, muxB, abs, imm, WE, Instr[15:9], WDmux
  // RegisterOpt registeropt_1: pin names not known; wires that end beside it: multiplexer_1_out, Clock, Instr[3:0], Instr[7:4], WE, registeropt_1_p6, D_out
  // ImReg imreg_1: pin names not known; wires that end beside it: Instr, imm, Clock, imreg_1_p4
  // SignExt signext_1: pin names not known; wires that end beside it: Instr, signext_1_p2, signext_1_p3, signext_1_p4
  Multiplexer #(.Bits(16)) multiplexer_2 (.sel(muxA), .in_0(registeropt_1_p6), .in_1(D_out), .out(multiplexer_2_out));
  Multiplexer #(.Selector_Bits(3), .Bits(16)) multiplexer_3 (
    .sel(muxB), .in_0(D_out), .in_1(imreg_1_p4), .in_2({16{1'b0}}), .in_3({16{1'b0}}), .in_4({16{1'b0}}),
    .in_5(signext_1_p2), .in_6(signext_1_p3), .in_7(signext_1_p4), .out(multiplexer_3_out));
  // Branch branch_1: pin names not known; wires that end beside it: pc_hdl_1_p5, br, branch_1_p3, branch_1_p4, branch_1_p5
  // ALU alu_1: pin names not known; wires that end beside it: multiplexer_2_out, ALUop, multiplexer_3_out, branch_1_p3, Addr, alu_1_p6, alu_1_p7, alu_1_p8
  // Flags flags_1: pin names not known; wires that end beside it: branch_1_p3, branch_1_p4, branch_1_p5, sf, Clock, alu_1_p8, alu_1_p7, alu_1_p6
  RAMDualPort #(.AddrBits(10), .Bits(16), .Addr_Bits(10)) ramdualport_1 (
    .A(Addr[9:0]), .Din(D_out), .str(st), .C(Clock), .ld(ld), .D(ramdualport_1_d));

  // Other names for the same wires on the sheet: C = Clock; res = reset

  // Notes on the sheet:
  //   Instr: Instruction
  //   {{de Befehlswort}}
  //   Clock: Hz: 200
  //   reset: reset input {{de Reset Eingang}}, default 1
  //   PC: Program Counter
  //   {{de Programzähler}}
  //   D_out: the data output for io writes
  //   {{de Datenbus für IO Ausgaben}}
  //   Addr: the address output used for io read and write
  //   {{de Adresse für IO Operationen.}}
  //   ioR: if high, a io read is performed 
  //   {{de IO Lesefreigabe}}
  //   ioW: if high, a io write is perfromed
  //   {{de IO Schreibfreigabe}}
  //   D_in: the data input for io reads
  //   {{de Datenbus für IO Leseoperationen.}}
endmodule
