// Digital circuit VGA.dig as structural Verilog
module VGA (
  input  RamClock,
  input  [15:0] D_in,
  input  str,
  input  ld,
  input  [15:0] A,
  input  PixClock,
  output [15:0] D,
  output sel,
  output H_sync,
  output V_sync,
  output [11:0] Col
);

  wire and_2_out, comparator_1_eq, core_1_h_sync, core_1_v_sync;
  wire [11:0] core_1_col;

  Comparator #(.Bits(4)) comparator_1 (.a(4'b1000), .b(A[15:12]), .eq(comparator_1_eq));  // open: gt, lt
  and and_1 (sel, ld, comparator_1_eq);
  and and_2 (and_2_out, str, comparator_1_eq);
  core core_1 (
    .ld(sel), .str(and_2_out), .A(A[11:0]), .D_in(D_in), .RamClock(RamClock), .PixClock(PixClock), .D(D),
    .H_sync(core_1_h_sync), .V_sync(core_1_v_sync), .Col(core_1_col));
  D_FF d_ff_1 (.D(core_1_h_sync), .C(PixClock), .Q(H_sync));  // open: nQ
  D_FF d_ff_2 (.D(core_1_v_sync), .C(PixClock), .Q(V_sync));  // open: nQ
  D_FF #(.Bits(12)) d_ff_3 (.D(core_1_col), .C(PixClock), .Q(Col));  // open: nQ

  // Notes on the sheet:
  //   RamClock: Hz: 25000000
  //   PixClock: Hz: 25000000
endmodule
