// Digital circuit core.dig as structural Verilog
module core (
  input  ld,
  input  str,
  input  [11:0] A,
  input  [15:0] D_in,
  input  RamClock,
  input  PixClock,
  output [15:0] D,
  output H_sync,
  output V_sync,
  output [11:0] Col
);

  wire sync_1_p2, sync_1_p3, sync_1_p4;
  wire [11:0] textmode_1_p9;

  // sync sync_1: pin names not known; wires that end beside it: PixClock, sync_1_p2, sync_1_p3, sync_1_p4, H_sync, V_sync
  // textMode textmode_1: pin names not known; wires that end beside it: D_in, str, ld, A, RamClock, sync_1_p2, sync_1_p3, D, textmode_1_p9
  Multiplexer #(.Bits(12)) multiplexer_1 (.sel(sync_1_p4), .in_0({12{1'b0}}), .in_1(textmode_1_p9), .out(Col));

  // Notes on the sheet:
  //   RamClock: Hz: 25000000
endmodule
