// Digital circuit VGAExample.dig as structural Verilog
module VGAExample (
  input  Clock,
  input  rst,
  input  U,
  input  D,
  input  R,
  input  L,
  output Y0,
  output Y1,
  output Y2,
  output Y3,
  output Y4,
  output Y5,
  output Y6,
  output Y7,
  output Y8,
  output Y9,
  output Y10,
  output Y11,
  output Y12,
  output Y13,
  output Y14,
  output Y15,
  output VGA_R0,
  output VGA_G0,
  output VGA_B0,
  output VGA_R1,
  output VGA_G1,
  output VGA_B1,
  output VGA_R2,
  output VGA_G2,
  output VGA_B2,
  output VGA_R3,
  output VGA_G3,
  output VGA_B3,
  output H_sync,
  output V_sync
);

  wire C, d_ff_1_nq, gpi_hdl_1_p7, gpi_hdl_1_p8, ioR, ioW, vga_1_sel;
  wire [15:0] A, Dout, processormux_1_pc, readselect_1_p9, ROM_d, vga_1_d;

  VGA vga_1 (
    .RamClock(C), .D_in(Dout), .str(ioW), .ld(ioR), .A(A), .PixClock(Clock), .D(vga_1_d), .sel(vga_1_sel),
    .H_sync(H_sync), .V_sync(V_sync),
    .Col({VGA_B3, VGA_B2, VGA_B1, VGA_B0, VGA_G3, VGA_G2, VGA_G1, VGA_G0, VGA_R3, VGA_R2, VGA_R1, VGA_R0}));
  // GPI_HDL gpi_hdl_1: pin names not known; wires that end beside it: A, ioR, U, L, R, D, gpi_hdl_1_p7, gpi_hdl_1_p8
  VGA vga_2 (
    .R({VGA_R3, VGA_R2, VGA_R1, VGA_R0}), .G({VGA_G3, VGA_G2, VGA_G1, VGA_G0}),
    .B({VGA_B3, VGA_B2, VGA_B1, VGA_B0}), .H(H_sync), .V(V_sync), .C(Clock));
  // readSelect readselect_1: pin names not known; wires that end beside it: gpi_hdl_1_p7, gpi_hdl_1_p8, vga_1_d, vga_1_sel, {16{1'b0}}, 1'b0, {16{1'b0}}, 1'b0, readselect_1_p9
  D_FF d_ff_1 (.D(d_ff_1_nq), .C(Clock), .Q(C), .nQ(d_ff_1_nq));
  ProcessorMux processormux_1 (
    .Instr(ROM_d), .Clock(C), .reset(rst), .D_in(readselect_1_p9), .PC(processormux_1_pc), .D_out(Dout),
    .Addr(A), .ioR(ioR), .ioW(ioW));
  ROM #(.AddrBits(16), .isProgramMemory("true"), .Bits(16), .Addr_Bits(16)) ROM (
    .A(processormux_1_pc), .sel(1'b1), .D(ROM_d));
  // GPO gpo_1: pin names not known; wires that end beside it: Y15, Y14, Y13, Y12, Y11, Y10, Y9, Y8, Y7, Y6, Y5, Y4, ioW, Y3, C, Y2, A, Y1, Dout, Y0

  // Other names for the same wires on the sheet: PC = Clock

  // Notes on the sheet:
  //   Clock: pin W5, Hz: 25175000
  //   Y0: pin U16
  //   Y1: pin E19
  //   Y2: pin U19
  //   Y3: pin V19
  //   Y4: pin W18
  //   Y5: pin U15
  //   Y6: pin U14
  //   Y7: pin V14
  //   Y8: pin V13
  //   Y9: pin V3
  //   Y10: pin W3
  //   Y11: pin U3
  //   Y12: pin P3
  //   Y13: pin N3
  //   Y14: pin P1
  //   Y15: pin L1
  //   rst: pin U18
  //   U: pin T18
  //   D: pin U17
  //   R: pin T17
  //   L: pin W19
  //   VGA_R0: pin G19
  //   VGA_G0: pin J17
  //   VGA_B0: pin N18
  //   VGA_R1: pin H19
  //   VGA_G1: pin H17
  //   VGA_B1: pin L18
  //   VGA_R2: pin J19
  //   VGA_G2: pin G17
  //   VGA_B2: pin K18
  //   VGA_R3: pin N19
  //   VGA_G3: pin D17
  //   VGA_B3: pin J18
  //   H_sync: pin P19
  //   V_sync: pin R19
  //   Pin numbers are defined to match the BASYS3 FPGA board.
  //   {{de Die Pin-Nummern sind angepasst an ein BASYS3 FPGA Board.}}
  //   contents of ROM (hex, n*v repeats v):
  //   1400,52c0,8020,1200,5250,8021,1200,52b0,8048,1200,5200,8057,1200,5260,8064,1200,52a0,
  //   8065,1200,5210,806c,1200,5220,5230,5290,806f,1200,5240,5270,8072,1200,5280,8028,1200,
  //   141f,1430,4e23,3c20,5e05,80aa,68f0,1831,1801,6ff8,b0cd,1220,1401,1410,80aa,68f0,151d,
  //   80aa,68f0,1801,8050,3a00,65f6,b0ba,1220,1411,1400,80aa,68f0,804f,1200,80aa,68f0,1811,
  //   3d1e,65f6,b0c9,1220,1400,1410,80aa,68f0,b0bb,1220,804f,1200,1410,80aa,68f0,b0c8,1220,
  //   1400,151d,80aa,68f0,b0bc,1220,804f,1200,151d,80aa,68f0,f000,1320,1411,1401,80aa,68f0,
  //   1821,1801,3d01,65fa,1811,3d11,65f6,7c00,141f,8027,1200,a002,1220,80a1,68f0,20e1,4ce4,
  //   809a,68f0,4e2e,18e1,80aa,68f0,79a4,56bd,52da,2ba,28b1,5e03,3c11,5e01,2011,2ba,28b2,
  //   5e03,3c01,5e01,2001,2ba,28b4,5e04,804e,3a00,5e01,1801,2ba,28b8,5fdb,3d1c,5fd9,1811,
  //   6fd7,14b5,14a0,20a1,65fe,20b1,65fc,6a0f,2a1,48a0,40a0,ea0,8000,17a0,7a4a,74a2,6a0f,
  //   2a1,48a0,40a0,ea0,8000,17a0,74a2,6a0f
endmodule
