// Digital circuit check code_odd 思考题3.dig as structural Verilog
module \check_code_odd_思考题3  (
  input  [6:0] A,
  input  [7:0] Y,
  output [7:0] Y_2,
  output Error
);

  wire xor_1_out, xor_2_out, xor_3_out, xor_4_out, xor_5_out, xor_6_out, xor_7_out, xor_9_out, xor_10_out,
       xor_11_out, xor_12_out, xor_13_out, xor_14_out;

  xor xor_1 (xor_1_out, 1'b1, A[0]);
  xor xor_2 (xor_2_out, A[1], A[2]);
  xor xor_3 (xor_3_out, A[3], A[4]);
  xor xor_4 (xor_4_out, A[5], A[6]);
  not not_1 (Error, xor_7_out);
  xor xor_5 (xor_5_out, xor_1_out, xor_2_out);
  xor xor_6 (xor_6_out, xor_3_out, xor_4_out);
  xor xor_7 (xor_7_out, xor_10_out, xor_9_out);
  xor xor_8 (Y_2[0], xor_5_out, xor_6_out);
  xor xor_9 (xor_9_out, xor_12_out, xor_11_out);
  xor xor_10 (xor_10_out, xor_14_out, xor_13_out);
  xor xor_11 (xor_11_out, Y[6], Y[7]);
  xor xor_12 (xor_12_out, Y[4], Y[5]);
  xor xor_13 (xor_13_out, Y[2], Y[3]);
  xor xor_14 (xor_14_out, Y[0], Y[1]);

  assign Y_2[7:1] = A;
endmodule
