// Digital circuit FullAdderRC_CLA.dig as structural Verilog
// Example to compare RC and CLA adders.
// {{de Beispiel um RC- und CLA-Addierer zu vergleichen.}}
module FullAdderRC_CLA (
  input  C0,
  input  A0,
  input  B0,
  input  A1,
  input  B1,
  input  A2,
  input  B2,
  input  A3,
  input  B3,
  input  A0_2,
  input  B0_2,
  input  C0_2,
  input  A1_2,
  input  B1_2,
  input  A2_2,
  input  B2_2,
  input  A3_2,
  input  B3_2,
  output S0,
  output S1,
  output S2,
  output C4,
  output S3,
  output S0_2,
  output S1_2,
  output S2_2,
  output S3_2,
  output C4_2
);

  wire add_2_c_o, add_3_c_o, add_4_c_o, and_5_out, and_6_out, and_7_out, and_8_out, and_9_out, and_10_out,
       and_11_out, and_12_out, and_13_out, and_14_out, G0, G1, G2, G3, or_1_out, or_2_out, or_3_out, P0, P1,
       P2, P3;

  Add add_1 (.a(A3), .b(B3), .c_i(add_2_c_o), .s(S3), .c_o(C4));
  Add add_2 (.a(A2), .b(B2), .c_i(add_3_c_o), .s(S2), .c_o(add_2_c_o));
  Add add_3 (.a(A1), .b(B1), .c_i(add_4_c_o), .s(S1), .c_o(add_3_c_o));
  Add add_4 (.a(A0), .b(B0), .c_i(C0), .s(S0), .c_o(add_4_c_o));
  xor xor_1 (P3, A3_2, B3_2);
  and and_1 (G3, A3_2, B3_2);
  xor xor_2 (P2, A2_2, B2_2);
  and and_2 (G2, A2_2, B2_2);
  xor xor_3 (P1, A1_2, B1_2);
  and and_3 (G1, A1_2, B1_2);
  xor xor_4 (P0, A0_2, B0_2);
  and and_4 (G0, A0_2, B0_2);
  and and_5 (and_5_out, G2, P3);
  and and_6 (and_6_out, G1, P3, P2);
  and and_7 (and_7_out, G0, P3, P2, P1);
  and and_8 (and_8_out, P3, P2, C0_2, P1, P0);
  and and_9 (and_9_out, G1, P2);
  and and_10 (and_10_out, G0, P2, P1);
  and and_11 (and_11_out, P2, P1, P0, C0_2);
  and and_12 (and_12_out, G0, P1);
  and and_13 (and_13_out, P1, P0, C0_2);
  and and_14 (and_14_out, P0, C0_2);
  or or_1 (or_1_out, G2, and_9_out, and_10_out, and_11_out);
  or or_2 (or_2_out, G1, and_12_out, and_13_out);
  or or_3 (or_3_out, G0, and_14_out);
  xor xor_5 (S0_2, P0, C0_2);
  or or_4 (C4_2, G3, and_5_out, and_6_out, and_7_out, and_8_out);
  // Probe C3 on or_1_out
  // Probe C2 on or_2_out
  // Probe C1 on or_3_out
  xor xor_6 (S3_2, P3, or_1_out);
  xor xor_7 (S2_2, P2, or_2_out);
  xor xor_8 (S1_2, P1, or_3_out);

  // Notes on the sheet:
  //   A0: default 1
  //   B1: default 1
  //   B2: default 1
  //   A3: default 1
  //   A0_2: default 1
  //   B1_2: default 1
  //   B2_2: default 1
  //   A3_2: default 1
endmodule

/* Test case Adder:
# A complete test of all 512 possible additions
# All created test vectors are shown in the result table.

C_{-1}  A3 A2 A1 A0  B3 B2 B1 B0  C S3 S2 S1 S0

loop(a,16)
 loop(b,16)
  0    bits(4,a)        bits(4,b)        bits(5,a+b)
  1    bits(4,a)        bits(4,b)        bits(5,a+b+1)
 end loop
end loop
*/
