// Digital circuit Division complement 思考题3.dig as structural Verilog
module \Division_complement_思考题3  (
  input  Y_3,
  input  X_0,
  input  X_1,
  input  X_2,
  input  X_3,
  input  X_4,
  input  X_5,
  input  X_6,
  input  Y_1,
  input  Y_2,
  input  Y_0,
  input  X_sign,
  input  Y_sign,
  output Q_0,
  output Q_1,
  output Q_2,
  output Q_3,
  output R_4,
  output R_5,
  output R_6,
  output Q_sign
);

  wire add_1_c_o, add_2_c_o, add_3_c_o, add_4_c_o, and_1_out, and_2_out, and_3_out, and_4_out, and_5_out,
       and_6_out, and_7_out, and_8_out, and_9_out, and_10_out, and_11_out, and_12_out, and_13_out,
       and_14_out, and_15_out, or_1_out, or_2_out, or_3_out, or_4_out, or_5_out, or_6_out, or_7_out,
       or_8_out, or_9_out, or_10_out, or_11_out, or_12_out, xor_1_out, xor_2_out, xor_3_out, xor_4_out;
  wire [0:0] xor_10_out, xor_11_out;
  wire [3:0] add_1_s, add_2_s, add_3_s, xor_8_out, xor_15_out, xor_19_out, xor_22_out, xor_24_out;
  wire [3:3] add_1_s_2, add_4_s;

  or or_1 (or_1_out, X_1, or_5_out);
  or or_2 (or_2_out, Y_1, or_3_out);
  or or_3 (or_3_out, Y_2, or_4_out);
  or or_4 (or_4_out, Y_3, 1'b0);
  or or_5 (or_5_out, X_2, or_6_out);
  or or_6 (or_6_out, X_3, or_7_out);
  or or_7 (or_7_out, X_4, or_8_out);
  or or_8 (or_8_out, X_5, or_9_out);
  and and_1 (and_1_out, Y_sign, or_2_out);
  and and_2 (and_2_out, Y_sign, or_3_out);
  and and_3 (and_3_out, Y_sign, or_4_out);
  and and_4 (and_4_out, Y_sign, 1'b0);
  or or_9 (or_9_out, X_6, 1'b0);
  xor xor_1 (xor_1_out, and_1_out, Y_0);
  xor xor_2 (xor_2_out, and_2_out, Y_1);
  xor xor_3 (xor_3_out, and_3_out, Y_2);
  xor xor_4 (xor_4_out, and_4_out, Y_3);
  and and_5 (and_5_out, X_sign, or_1_out);
  and and_6 (and_6_out, X_sign, or_5_out);
  and and_7 (and_7_out, X_sign, or_6_out);
  and and_8 (and_8_out, X_sign, or_7_out);
  and and_9 (and_9_out, X_sign, or_8_out);
  and and_10 (and_10_out, X_sign, or_9_out);
  and and_11 (and_11_out, X_sign, 1'b0);
  xor xor_5 (xor_8_out[3], and_5_out, X_0);
  xor xor_6 (xor_8_out[2], and_6_out, X_1);
  xor xor_7 (xor_8_out[1], and_7_out, X_2);
  xor xor_8 (xor_8_out[0], and_8_out, X_3);
  xor xor_9 (add_1_s[0], and_9_out, X_4);
  xor xor_10 (xor_10_out[0], and_10_out, X_5);
  xor xor_11 (xor_11_out[0], and_11_out, X_6);
  xor xor_12 (xor_15_out[0], xor_4_out, 1'b1);
  xor xor_13 (xor_15_out[1], xor_3_out, 1'b1);
  xor xor_14 (xor_15_out[2], xor_2_out, 1'b1);
  xor xor_15 (xor_15_out[3], xor_1_out, 1'b1);
  Add #(.Bits(4)) add_1 (.a(xor_8_out), .b(xor_15_out), .c_i(1'b1), .s({add_1_s_2[3], add_1_s[3:1]}), .c_o(add_1_c_o));
  xor xor_16 (xor_19_out[0], add_1_c_o, xor_4_out);
  xor xor_17 (xor_19_out[1], add_1_c_o, xor_3_out);
  xor xor_18 (xor_19_out[2], add_1_c_o, xor_2_out);
  xor xor_19 (xor_19_out[3], add_1_c_o, xor_1_out);
  Add #(.Bits(4)) add_2 (.a(add_1_s), .b(xor_19_out), .c_i(add_1_c_o), .s(add_2_s), .c_o(add_2_c_o));
  xor xor_20 (xor_22_out[0], add_2_c_o, xor_4_out);
  xor xor_21 (xor_22_out[1], add_2_c_o, xor_3_out);
  xor xor_22 (xor_22_out[2], add_2_c_o, xor_2_out);
  xor xor_23 (xor_22_out[3], add_2_c_o, xor_1_out);
  Add #(.Bits(4)) add_3 (
    .a({add_2_s[2:0], xor_10_out[0]}), .b(xor_22_out), .c_i(add_2_c_o), .s(add_3_s), .c_o(add_3_c_o));
  xor xor_24 (xor_24_out[0], add_3_c_o, xor_4_out);
  xor xor_25 (xor_24_out[1], add_3_c_o, xor_3_out);
  xor xor_26 (xor_24_out[2], add_3_c_o, xor_2_out);
  xor xor_27 (xor_24_out[3], add_3_c_o, xor_1_out);
  Add #(.Bits(4)) add_4 (
    .a({add_3_s[2:0], xor_11_out[0]}), .b(xor_24_out), .c_i(add_3_c_o), .s({add_4_s[3], R_4, R_5, R_6}),
    .c_o(add_4_c_o));
  or or_10 (or_10_out, add_2_c_o, or_11_out);
  or or_11 (or_11_out, add_3_c_o, or_12_out);
  or or_12 (or_12_out, add_4_c_o, 1'b0);
  xor xor_28 (Q_sign, X_sign, Y_sign);
  and and_12 (and_12_out, Q_sign, or_10_out);
  and and_13 (and_13_out, Q_sign, or_11_out);
  and and_14 (and_14_out, Q_sign, or_12_out);
  and and_15 (and_15_out, Q_sign, 1'b0);
  xor xor_29 (Q_0, and_12_out, add_1_c_o);
  xor xor_30 (Q_1, and_13_out, add_2_c_o);
  xor xor_31 (Q_2, and_14_out, add_3_c_o);
  xor xor_32 (Q_3, and_15_out, add_4_c_o);

  // Other names for the same wires on the sheet: Xsign = X_sign; Ysign = Y_sign

  // Notes on the sheet:
  //   Q_0: The result of the multiply operation.
  //   {{de Das 8-Bit Ergebnis der Multiplikation}}
endmodule
