// Digital circuit FullAdderRC_CLA BUS版.dig as structural Verilog
module \FullAdderRC_CLA_BUS版  (
  input  clk,
  input  M,
  input  A0,
  input  B0,
  input  A1,
  input  B1,
  input  A2,
  input  B2,
  input  A3,
  input  B3,
  output S0,
  output S1,
  output S2,
  output C4,
  output S3
);

  wire A0_t, A1_t, A2_t, A3_t, add_2_c_o, add_3_c_o, add_4_c_o, and_5_out, and_6_out, and_7_out, and_8_out,
       and_9_out, and_10_out, and_11_out, and_12_out, and_13_out, and_14_out, B0_t, B1_t, B2_t, B3_t, C1, C2,
       C3, C4_t, G0, G1, G2, G3, M_t, P0, P1, P2, P3, S0_t, S1_t, S2_t, S3_t, xor_1_out, xor_2_out,
       xor_3_out, xor_4_out, xor_5_out, xor_6_out, xor_7_out, xor_8_out;
  wire [31:9] bus_1_p3;

  xor xor_1 (xor_1_out, M, B3);
  xor xor_2 (xor_2_out, M, B2);
  xor xor_3 (xor_3_out, M, B1);
  xor xor_4 (xor_4_out, M, B0);
  Add add_1 (.a(A3), .b(xor_1_out), .c_i(add_2_c_o), .s(S3), .c_o(C4));
  Add add_2 (.a(A2), .b(xor_2_out), .c_i(add_3_c_o), .s(S2), .c_o(add_2_c_o));
  Add add_3 (.a(A1), .b(xor_3_out), .c_i(add_4_c_o), .s(S1), .c_o(add_3_c_o));
  Add add_4 (.a(A0), .b(xor_4_out), .c_i(M), .s(S0), .c_o(add_4_c_o));
  xor xor_5 (xor_5_out, M_t, B3_t);
  xor xor_6 (xor_6_out, M_t, B2_t);
  xor xor_7 (xor_7_out, M_t, B1_t);
  xor xor_8 (xor_8_out, M_t, B0_t);
  xor xor_9 (P3, A3_t, xor_5_out);
  and and_1 (G3, A3_t, xor_5_out);
  xor xor_10 (P2, A2_t, xor_6_out);
  and and_2 (G2, A2_t, xor_6_out);
  xor xor_11 (P1, A1_t, xor_7_out);
  and and_3 (G1, A1_t, xor_7_out);
  xor xor_12 (P0, A0_t, xor_8_out);
  and and_4 (G0, A0_t, xor_8_out);
  // Bus bus_1: pin names not known; wires that end beside it: clk, {{23{1'b0}}, C4_t, 4'b0000, S3_t, S2_t, S1_t, S0_t}, {bus_1_p3, M_t, B3_t, B2_t, B1_t, B0_t, A3_t, A2_t, A1_t, A0_t}
  and and_5 (and_5_out, G2, P3);
  and and_6 (and_6_out, G1, P3, P2);
  and and_7 (and_7_out, G0, P3, P2, P1);
  and and_8 (and_8_out, P3, P2, M_t, P1, P0);
  and and_9 (and_9_out, G1, P2);
  and and_10 (and_10_out, G0, P2, P1);
  and and_11 (and_11_out, P2, P1, P0, M_t);
  and and_12 (and_12_out, G0, P1);
  and and_13 (and_13_out, P1, P0, M_t);
  and and_14 (and_14_out, P0, M_t);
  or or_1 (C4_t, G3, and_5_out, and_6_out, and_7_out, and_8_out);
  or or_2 (C3, G2, and_9_out, and_10_out, and_11_out);
  or or_3 (C2, G1, and_12_out, and_13_out);
  or or_4 (C1, G0, and_14_out);
  xor xor_13 (S0_t, P0, M_t);
  // Probe on C4_t
  xor xor_14 (S3_t, P3, C3);
  xor xor_15 (S2_t, P2, C2);
  xor xor_16 (S1_t, P1, C1);

  // Notes on the sheet:
  //   clk: Hz: 10
  //   A0: default 1
  //   B1: default 1
  //   B2: default 1
  //   A3: default 1
endmodule

/* Test case:
A_1 A_0 D Y_3 Y_2 Y_1 Y_0
 0   0  0  0   0   0   0
 0   0  1  0   0   0   1
 0   1  0  0   0   0   0
 0   1  1  0   0   1   0
 1   0  0  0   0   0   0
 1   0  1  0   1   0   0
 1   1  0  0   0   0   0
 1   1  1  1   0   0   0
*/
