// Digital circuit absolute 思考题2.dig as structural Verilog
module \absolute_思考题2  (
  input  P_0,
  input  P_1,
  input  P_2,
  input  P_3,
  input  P_sign,
  input  P_4,
  input  P_5,
  input  P_6,
  input  P_7,
  output Q0,
  output Q1,
  output Q2,
  output Q3,
  output Q_sign,
  output Q4,
  output Q5,
  output Q6,
  output Q_7
);

  wire and_1_out, and_2_out, and_3_out, and_4_out, and_5_out, and_6_out, and_7_out, and_8_out, or_1_out,
       or_2_out, or_3_out, or_4_out, or_5_out, or_6_out, or_7_out;

  or or_1 (or_1_out, P_6, or_2_out);
  or or_2 (or_2_out, P_5, or_3_out);
  or or_3 (or_3_out, P_4, or_4_out);
  or or_4 (or_4_out, P_3, or_5_out);
  or or_5 (or_5_out, P_2, or_6_out);
  or or_6 (or_6_out, P_1, or_7_out);
  or or_7 (or_7_out, P_0, 1'b0);
  and and_1 (and_1_out, P_sign, or_1_out);
  and and_2 (and_2_out, P_sign, or_2_out);
  and and_3 (and_3_out, P_sign, or_3_out);
  and and_4 (and_4_out, P_sign, or_4_out);
  and and_5 (and_5_out, P_sign, or_5_out);
  and and_6 (and_6_out, P_sign, or_6_out);
  and and_7 (and_7_out, P_sign, or_7_out);
  and and_8 (and_8_out, P_sign, 1'b0);
  xor xor_1 (Q_7, and_1_out, P_7);
  xor xor_2 (Q6, and_2_out, P_6);
  xor xor_3 (Q5, and_3_out, P_5);
  xor xor_4 (Q4, and_4_out, P_4);
  xor xor_5 (Q3, and_5_out, P_3);
  xor xor_6 (Q2, and_6_out, P_2);
  xor xor_7 (Q1, and_7_out, P_1);
  xor xor_8 (Q0, and_8_out, P_0);

  assign Q_sign = 1'b0;

  // Notes on the sheet:
  //   P_0: First number to multiply.
  //   {{de Erste zu multiplizierende 4 Bit Zahl.}}
endmodule
