// Digital circuit ROM&RAM 思考题1.dig as structural Verilog
module \ROM_RAM_思考题1  (
  input  [11:0] Addr,
  input  [7:0] Din,
  input  WE,
  input  Clk,
  output [7:0] Dout
);

  wire and_1_out, comparator_1_eq, comparator_2_eq;
  wire [7:0] ramdualport_1_d, rom_d;

  and and_1 (and_1_out, WE, comparator_1_eq);
  Comparator #(.Bits(3)) comparator_1 (.a(Addr[11:9]), .b(3'b011), .eq(comparator_1_eq));  // open: gt, lt
  Comparator #(.Bits(4)) comparator_2 (.a(Addr[11:8]), .b(4'b1000), .eq(comparator_2_eq));  // open: gt, lt
  ROM #(.AddrBits(8), .Bits(8)) rom (.A(Addr[7:0]), .sel(comparator_2_eq), .D(rom_d));
  RAMDualPort #(.AddrBits(9), .Bits(8)) ramdualport_1 (
    .A(Addr[8:0]), .Din(Din), .str(and_1_out), .C(Clk), .ld(comparator_1_eq), .D(ramdualport_1_d));
  Multiplexer #(.Bits(8)) multiplexer_1 (.sel(comparator_2_eq), .in_0(ramdualport_1_d), .in_1(rom_d), .out(Dout));

  // Notes on the sheet:
  //   Addr: A
  //   contents of rom (hex, n*v repeats v):
  //   f,0,0,0,0,0,f,0,0,0,0,0,0,0,0,0,0,0,0,0,0,0,0,0,0,0,0,0,0,0,0,1
endmodule
