// Digital circuit microprogram-I.dig as structural Verilog
module microprogram_I (
  input  clock,
  input  hand,
  input  model,
  input  reset
);

  wire and_2_out, and_3_out, break_q, clk, hlt, I_0, LDPC, multiplexer_3_out, nor_1_out, P1, PC_INC;
  wire [3:0] counter_1_out, MAR_q, multiplexer_2_out, OP;
  wire [3:1] ROM_d;
  wire [7:0] add_1_s, multiplexer_1_out, PC_q;
  wire [15:0] MROM_d;

  Multiplexer #(.Bits(8)) multiplexer_1 (.sel(LDPC), .in_0(add_1_s), .in_1({OP, ROM_d, I_0}), .out(multiplexer_1_out));
  Multiplexer #(.Bits(4)) multiplexer_2 (.sel(P1), .in_0(MROM_d[3:0]), .in_1(OP), .out(multiplexer_2_out));
  // Probe on multiplexer_1_out
  Register #(.Bits(8)) PC (.D(multiplexer_1_out), .C(clk), .en(PC_INC), .Q(PC_q));
  // Probe on multiplexer_2_out
  nor nor_1 (nor_1_out, OP[0], OP[1], OP[2], OP[3]);
  Multiplexer multiplexer_3 (.sel(model), .in_0(hand), .in_1(clock), .out(multiplexer_3_out));
  Register #(.Bits(4)) MAR (.D(multiplexer_2_out), .C(clk), .en(1'b1), .Q(MAR_q));
  and and_1 (hlt, P1, nor_1_out, I_0);
  or or_1 (clk, multiplexer_3_out, break_q);
  Add #(.Bits(8)) add_1 (.a(8'h1), .b(PC_q), .c_i(1'b0), .s(add_1_s));  // open: c_o
  // Probe on MAR_q
  ROM #(.AddrBits(4), .Bits(16), .Addr_Bits(6)) MROM (
    .A(MAR_q), .sel(1'b1), .D({MROM_d[15:13], LDPC, MROM_d[11:9], PC_INC, MROM_d[7:6], P1, MROM_d[4:0]}));
  // Probe on PC_q
  ROM #(.AddrBits(8), .Bits(8)) ROM (.A(PC_q), .sel(1'b1), .D({OP, ROM_d, I_0}));
  // Probe on PC_q
  // Probe on {MROM_d[15:13], LDPC, MROM_d[11:9], PC_INC, MROM_d[7:6], P1, MROM_d[4:0]}
  and and_2 (and_2_out, reset, multiplexer_3_out);
  // Probe on MROM_d[3:0]
  // Probe on {OP, ROM_d, I_0}
  // Probe on OP
  and and_3 (and_3_out, ~clk, P1);  // And
  Counter #(.Bits(4)) counter_1 (.en(1'b1), .C(and_3_out), .clr(1'b0), .out(counter_1_out));  // open: ovf
  D_FF_AS \break  (.Set(1'b0), .D(hlt), .C(clk), .Clr(and_2_out), .Q(break_q));  // open: nQ
  Seven_Seg_Hex seven_seg_hex_1 (.d(counter_1_out), .dp(1'b0));
  LED led_1 (.in(break_q));

  // Notes on the sheet:
  //   clock: Hz: 2
  //   微程序控制器
  //   contents of MROM (hex, n*v repeats v):
  //   120,1100
  //   contents of ROM (hex, n*v repeats v):
  //   10,3,0,1,10,2
endmodule
