// Digital circuit hard logic-II 课程设计1.dig as structural Verilog
module \hard_logic_II_课程设计1  (
  input  [7:0] IN,
  input  clock,
  input  hand,
  input  model,
  input  reset,
  output [7:0] OUT
);

  wire and_1_out, and_3_out, and_6_out, break_q, clk, ENout, hlt, I_0, I_10, LDPC, M1, M2, memw,
       multiplexer_2_out, nand_1_out, NOP, P2, PC_INC, PC_plus_1, regw;
  wire [1:0] Asel, Ra, Rb;
  wire [2:0] Ssel;
  wire [3:0] counter_1_out, OP;
  wire [7:0] add_1_s, bitextender_1_out, Da, Db, Dram_d, Drom_d, Min, Mout, multiplexer_1_out,
       multiplexer_3_out, multiplexer_5_out, out_t, PC_q, register_1_q, Rin;
  wire [7:1] IMM;

  // Probe on {IMM, I_0}
  Multiplexer #(.Bits(8)) multiplexer_1 (.sel(LDPC), .in_0(add_1_s), .in_1({IMM, I_0}), .out(multiplexer_1_out));
  // Probe on multiplexer_1_out
  Register #(.Bits(8)) PC (.D(multiplexer_1_out), .C(clk), .en(PC_plus_1), .Q(PC_q));
  Add #(.Bits(8)) add_1 (.a(8'h1), .b(PC_q), .c_i(1'b0), .s(add_1_s));  // open: c_o
  D_FF M (.D(and_1_out), .C(clk), .Q(M2), .nQ(M1));
  and and_1 (and_1_out, ~NOP, M1);  // And
  LED u_M1 (.in(M1));
  LED u_M2 (.in(M2));
  Multiplexer multiplexer_2 (.sel(model), .in_0(hand), .in_1(clock), .out(multiplexer_2_out));
  ROM #(.AddrBits(8), .Bits(8)) ROM (.A(PC_q), .sel(1'b1), .D({IMM, I_0}));
  // Probe on PC_q
  or or_1 (clk, multiplexer_2_out, break_q);
  BitExtender #(.inputBits(1), .outputBits(8)) bitextender_1 (.in(M2), .out(bitextender_1_out));
  // logic_II logic_ii_1: pin names not known; wires that end beside it: OP, LDPC, PC_INC, P2, Ssel, Asel
  and and_2 (hlt, I_0, NOP, M1);
  nor nor_1 (NOP, IMM[4], IMM[5], IMM[6], IMM[7]);
  Register #(.Bits(8)) register_1 (.D({IMM, I_0}), .C(clk), .en(M1), .Q(register_1_q));
  and and_3 (and_3_out, reset, multiplexer_2_out);
  assign {OP, Ra, Rb} = register_1_q & bitextender_1_out;  // And and_4, 8 bits wide
  // Probe on {OP, Ra, Rb}
  Counter #(.Bits(4)) counter_1 (.en(1'b1), .C(M1), .clr(1'b0), .out(counter_1_out));  // open: ovf
  D_FF_AS \break  (.Set(1'b0), .D(hlt), .C(clk), .Clr(and_3_out), .Q(break_q));  // open: nQ
  Seven_Seg_Hex seven_seg_hex_1 (.d(counter_1_out), .dp(1'b0));
  LED led_1 (.in(break_q));
  nand nand_1 (nand_1_out, I_10, P2);
  and and_5 (PC_plus_1, nand_1_out, PC_INC);
  or or_2 (I_10, Rb[0], Rb[1]);
  Multiplexer #(.Bits(8)) multiplexer_3 (.sel(I_10), .in_0({IMM, I_0}), .in_1(Db), .out(multiplexer_3_out));
  and and_6 (and_6_out, memw, ~multiplexer_3_out[7]);  // And
  // Probe on Min
  RAMDualPort #(.AddrBits(7), .Bits(8)) Dram (
    .A(multiplexer_3_out[6:0]), .Din(Min), .str(and_6_out), .C(clk), .ld(1'b1), .D(Dram_d));
  ROM #(.AddrBits(7), .Bits(8)) Drom (.A(multiplexer_3_out[6:0]), .sel(1'b1), .D(Drom_d));
  Register #(.Bits(8)) register_2 (.D(out_t), .C(clk), .en(ENout), .Q(OUT));
  // Probe on Rin
  RegisterFile #(.Bits(8)) regs (.Din(Rin), .we(regw), .Rw(Ra), .C(clk), .Ra(Ra), .Rb(Rb), .Da(Da), .Db(Db));
  Multiplexer #(.Bits(8)) multiplexer_4 (.sel(multiplexer_3_out[7]), .in_0(Dram_d), .in_1(Drom_d), .out(Mout));
  // Probe on Da
  // Probe on Db
  // Probe on Mout
  LED led_2 (.in(OUT[7]));
  Multiplexer #(.Selector_Bits(3), .Bits(8)) multiplexer_5 (
    .sel(Ssel), .in_0({8{1'b0}}), .in_1(Da), .in_2(Mout), .in_3(IN), .in_4({IMM, I_0}), .in_5(Db),
    .in_6({8{1'b0}}), .in_7({8{1'b0}}), .out(multiplexer_5_out));
  // Probe on Ssel
  Decoder #(.Selector_Bits(2)) decoder_1 (.sel(Asel), .out_1(regw), .out_2(memw), .out_3(ENout));  // open: out_0
  // Probe on Asel
  Demultiplexer #(.Selector_Bits(2), .Bits(8)) demultiplexer_1 (
    .sel(Asel), .in(multiplexer_5_out), .out_1(Rin), .out_2(Min), .out_3(out_t));  // open: out_0

  // Other names for the same wires on the sheet: IMM[0] = I_0

  // Notes on the sheet:
  //   clock: Hz: 2
  //   硬布线控制器
  //   contents of ROM (hex, n*v repeats v):
  //   30,4,34,3,4c,5c,74,3,28,72,60,3,66,1
  //   存储器
  //   寄存器
  //   contents of Drom (hex, n*v repeats v):
  //   0,fffff0b7,400093,40016f,158513,feb50fe3,fff20193,318233,308023,309023,30a023,40a223,
  //   402383,800403,801403,804403,805403,802403,ff3a413,ffe3b413,fff44413,247493,249513,
  //   1f4d593,25d593,40125613,40460633,c616b3,c42733,c43733,864733,e6d7b3,40f75733,d77733,
  //   c76833,200713,11d873,11d873,810f3,710f3,a973,25973,1039f3,10f9f3,e7
  //   数据通路
  //   bus
endmodule
