// Digital circuit microprogram-I BUS版.dig as structural Verilog
module \microprogram_I_BUS版  (
  input  clock,
  input  hand,
  input  model,
  input  reset,
  input  clk
);

  wire and_2_out, and_3_out, break_q, clk_t, hlt, I_0, LDPC, multiplexer_3_out, nor_1_out;
  wire [3:0] counter_1_out, MAR, multiplexer_2_out;
  wire [7:0] add_1_s, multiplexer_1_out, PC;
  wire [7:1] IMM;
  wire [15:0] MDR;

  Multiplexer #(.Bits(8)) multiplexer_1 (.sel(LDPC), .in_0(add_1_s), .in_1({IMM, I_0}), .out(multiplexer_1_out));
  Multiplexer #(.Bits(4)) multiplexer_2 (.sel(MDR[5]), .in_0(MDR[3:0]), .in_1(IMM[7:4]), .out(multiplexer_2_out));
  // Probe on multiplexer_1_out
  Register #(.Bits(8)) u_PC (.D(multiplexer_1_out), .C(clk_t), .en(MDR[8]), .Q(PC));
  // Probe on multiplexer_2_out
  nor nor_1 (nor_1_out, IMM[4], IMM[5], IMM[6], IMM[7]);
  Multiplexer multiplexer_3 (.sel(model), .in_0(hand), .in_1(clock), .out(multiplexer_3_out));
  Register #(.Bits(4)) u_MAR (.D(multiplexer_2_out), .C(clk_t), .en(1'b1), .Q(MAR));
  and and_1 (hlt, MDR[5], nor_1_out, I_0);
  or or_1 (clk_t, multiplexer_3_out, break_q);
  Add #(.Bits(8)) add_1 (.a(8'h1), .b(PC), .c_i(1'b0), .s(add_1_s));  // open: c_o
  // Probe on MAR
  ROM #(.AddrBits(4), .Bits(16), .Addr_Bits(6)) MROM (.A(MAR), .sel(1'b1), .D({MDR[15:13], LDPC, MDR[11:0]}));
  // Probe on PC
  ROM #(.AddrBits(8), .Bits(8)) ROM (.A(PC), .sel(1'b1), .D({IMM, I_0}));
  // Probe on PC
  // Probe on {MDR[15:13], LDPC, MDR[11:0]}
  and and_2 (and_2_out, reset, multiplexer_3_out);
  // Probe on MDR[3:0]
  // Probe on {IMM, I_0}
  // Probe on IMM[7:4]
  and and_3 (and_3_out, ~clk_t, MDR[5]);  // And
  Counter #(.Bits(4)) counter_1 (.en(1'b1), .C(and_3_out), .clr(1'b0), .out(counter_1_out));  // open: ovf
  D_FF_AS \break  (.Set(1'b0), .D(hlt), .C(clk_t), .Clr(and_2_out), .Q(break_q));  // open: nQ
  Seven_Seg_Hex seven_seg_hex_1 (.d(counter_1_out), .dp(1'b0));
  LED led_1 (.in(break_q));
  // Bus bus_1: pin names not known; wires that end beside it: clk, {MDR[15:13], LDPC, MDR[11:0], IMM, I_0, MAR, PC[3:0]}

  // Other names for the same wires on the sheet: IMM[0] = I_0; OP[3:0] = IMM[7:4]; P1 = MDR[5]; PC_INC = MDR[8];
  //   MDR[12] = LDPC

  // Notes on the sheet:
  //   clock: Hz: 2
  //   clk: Hz: 10
  //   微程序控制器
  //   contents of MROM (hex, n*v repeats v):
  //   120,1100
  //   contents of ROM (hex, n*v repeats v):
  //   10,3,0,1,10,2
endmodule
