// Digital circuit microprogram-II BUS版.dig as structural Verilog
module \microprogram_II_BUS版  (
  input  clock,
  input  hand,
  input  model,
  input  reset,
  input  clk,
  output [7:0] OUT
);

  wire and_2_out, and_4_out, break_q, clk_t, ENout, hlt, I_0, I_10, LDPC, memw, multiplexer_3_out,
       nand_1_out, nor_1_out, PC_plus_1, regw;
  wire [1:0] Asel, Ra, Rb;
  wire [3:0] counter_1_out, MAR, multiplexer_2_out;
  wire [7:0] add_1_s, Da, Db, Dram_d, Drom_d, in, Min, Mout, multiplexer_1_out, multiplexer_4_out,
       multiplexer_6_out, out_t, PC, Rin;
  wire [7:1] IMM;
  wire [15:0] MDR;
  wire [31:8] bus_1_p3;

  Multiplexer #(.Bits(8)) multiplexer_1 (.sel(LDPC), .in_0(add_1_s), .in_1({IMM, I_0}), .out(multiplexer_1_out));
  Multiplexer #(.Bits(4)) multiplexer_2 (.sel(MDR[5]), .in_0(MDR[3:0]), .in_1(IMM[7:4]), .out(multiplexer_2_out));
  // Probe on multiplexer_1_out
  Register #(.Bits(8)) u_PC (.D(multiplexer_1_out), .C(clk_t), .en(PC_plus_1), .Q(PC));
  // Probe on multiplexer_2_out
  nor nor_1 (nor_1_out, IMM[4], IMM[5], IMM[6], IMM[7]);
  Multiplexer multiplexer_3 (.sel(model), .in_0(hand), .in_1(clock), .out(multiplexer_3_out));
  Register #(.Bits(4)) u_MAR (.D(multiplexer_2_out), .C(clk_t), .en(1'b1), .Q(MAR));
  and and_1 (hlt, MDR[5], nor_1_out, I_0);
  or or_1 (clk_t, multiplexer_3_out, break_q);
  Add #(.Bits(8)) add_1 (.a(8'h1), .b(PC), .c_i(1'b0), .s(add_1_s));  // open: c_o
  // Probe on MAR
  ROM #(.AddrBits(4), .Bits(16), .Addr_Bits(6)) MROM (
    .A(MAR), .sel(1'b1), .D({MDR[15:13], LDPC, MDR[11:8], Asel, MDR[5:0]}));
  // Probe on PC
  ROM #(.AddrBits(8), .Bits(8)) ROM (.A(PC), .sel(1'b1), .D({IMM, I_0}));
  // Probe on PC
  // Probe on {MDR[15:13], LDPC, MDR[11:8], Asel, MDR[5:0]}
  and and_2 (and_2_out, reset, multiplexer_3_out);
  // Probe on MDR[3:0]
  // Probe on {IMM, I_0}
  // Probe on IMM[7:4]
  Register #(.Bits(4)) register_1 (.D({IMM[3:1], I_0}), .C(clk_t), .en(MDR[5]), .Q({Ra, Rb}));
  Counter #(.Bits(4)) counter_1 (.en(1'b1), .C(MDR[5]), .clr(1'b0), .out(counter_1_out));  // open: ovf
  D_FF_AS \break  (.Set(1'b0), .D(hlt), .C(clk_t), .Clr(and_2_out), .Q(break_q));  // open: nQ
  // Probe on Rb
  // Probe on Ra
  Seven_Seg_Hex seven_seg_hex_1 (.d(counter_1_out), .dp(1'b0));
  LED led_1 (.in(break_q));
  nand nand_1 (nand_1_out, I_10, MDR[4]);
  and and_3 (PC_plus_1, nand_1_out, MDR[8]);
  or or_2 (I_10, Rb[0], Rb[1]);
  Multiplexer #(.Bits(8)) multiplexer_4 (.sel(I_10), .in_0({IMM, I_0}), .in_1(Db), .out(multiplexer_4_out));
  and and_4 (and_4_out, memw, ~multiplexer_4_out[7]);  // And
  // Probe on Min
  RAMDualPort #(.AddrBits(7), .Bits(8)) Dram (
    .A(multiplexer_4_out[6:0]), .Din(Min), .str(and_4_out), .C(clk_t), .ld(1'b1), .D(Dram_d));
  ROM #(.AddrBits(7), .Bits(8)) Drom (.A(multiplexer_4_out[6:0]), .sel(1'b1), .D(Drom_d));
  // Probe on Rin
  RegisterFile #(.Bits(8)) regs (.Din(Rin), .we(regw), .Rw(Ra), .C(clk_t), .Ra(Ra), .Rb(Rb), .Da(Da), .Db(Db));
  Multiplexer #(.Bits(8)) multiplexer_5 (.sel(multiplexer_4_out[7]), .in_0(Dram_d), .in_1(Drom_d), .out(Mout));
  // Probe on Da
  // Probe on Db
  // Probe on Mout
  Multiplexer #(.Selector_Bits(3), .Bits(8)) multiplexer_6 (
    .sel(MDR[11:9]), .in_0({8{1'b0}}), .in_1(Da), .in_2(Mout), .in_3(in), .in_4({IMM, I_0}), .in_5(Db),
    .in_6({8{1'b0}}), .in_7({8{1'b0}}), .out(multiplexer_6_out));
  // Probe on MDR[11:9]
  Register #(.Bits(8)) register_2 (.D(out_t), .C(clk_t), .en(ENout), .Q(OUT));
  // Bus bus_1: pin names not known; wires that end beside it: clk, {MDR[15:13], LDPC, MDR[11:8], Asel, MDR[5:0], IMM, I_0, MAR, PC[3:0]}, {bus_1_p3, in}
  Decoder #(.Selector_Bits(2)) decoder_1 (.sel(Asel), .out_1(regw), .out_2(memw), .out_3(ENout));  // open: out_0
  // Probe on Asel
  Demultiplexer #(.Selector_Bits(2), .Bits(8)) demultiplexer_1 (
    .sel(Asel), .in(multiplexer_6_out), .out_1(Rin), .out_2(Min), .out_3(out_t));  // open: out_0
  LED led_2 (.in(OUT[7]));
  // Probe on in

  // Other names for the same wires on the sheet: IMM[0] = I_0; OP[3:0] = IMM[7:4]; P2 = MDR[4]; P1 = MDR[5];
  //   MDR (some bits) = {LDPC, Asel}; PC_INC = MDR[8]; Ssel[2:0] = MDR[11:9]

  // Notes on the sheet:
  //   clock: Hz: 2
  //   clk: Hz: 10
  //   微程序控制器
  //   contents of MROM (hex, n*v repeats v):
  //   120,1100,a40,940,640,2c0,550,390
  //   contents of ROM (hex, n*v repeats v):
  //   30,4,34,3,4c,5c,74,3,28,72,60,3,66,1
  //   存储器
  //   寄存器
  //   contents of Drom (hex, n*v repeats v):
  //   0,fffff0b7,400093,40016f,158513,feb50fe3,fff20193,318233,308023,309023,30a023,40a223,
  //   402383,800403,801403,804403,805403,802403,ff3a413,ffe3b413,fff44413,247493,249513,
  //   1f4d593,25d593,40125613,40460633,c616b3,c42733,c43733,864733,e6d7b3,40f75733,d77733,
  //   c76833,200713,11d873,11d873,810f3,710f3,a973,25973,1039f3,10f9f3,e7
  //   数据通路
  //   bus
endmodule
