// Digital circuit microprogram-III BUS版.dig as structural Verilog
module \microprogram_III_BUS版  (
  input  clk,
  input  clock,
  input  hand,
  input  model,
  input  reset,
  output [7:0] OUT
);

  wire and_1_out, and_3_out, and_5_out, break_q, C, C_F, clk_t, ENout, hlt, I_0, I_10, LDPC, memw,
       multiplexer_1_out, multiplexer_4_out, nand_1_out, nor_1_out, PC_plus_1, regw, S, S_F, Z, Z_F;
  wire [1:0] Asel, Ra, Rb;
  wire [2:0] ALUop;
  wire [3:0] counter_1_out, MAR, multiplexer_3_out;
  wire [6:0] multiplexer_8_out;
  wire [7:0] add_1_s, add_2_s, and_6_out, barrelshifter_1_out, barrelshifter_2_out, barrelshifter_3_out,
       barrelshifter_4_out, Da, Db, Dram_d, Drom_d, in, Min, Mout, mul_1_mul, multiplexer_2_out,
       multiplexer_9_out, or_3_out, out_t, PC, Rin, sub_1_s, Xin, xor_1_out, Yin;
  wire [7:1] IMM;
  wire [11:0] MDR;
  wire [15:8] mul_1_mul_2;
  wire [31:8] bus_1_p3;

  Multiplexer #(.Selector_Bits(2)) multiplexer_1 (
    .sel(Rb), .in_0(1'b1), .in_1(C), .in_2(Z), .in_3(S), .out(multiplexer_1_out));
  Register #(.Bits(3)) ALU_Flag (.D({S_F, Z_F, C_F}), .C(MDR[5]), .en(1'b1), .Q({S, Z, C}));
  and and_1 (and_1_out, multiplexer_1_out, LDPC);
  Multiplexer #(.Bits(8)) multiplexer_2 (.sel(and_1_out), .in_0(add_1_s), .in_1({IMM, I_0}), .out(multiplexer_2_out));
  // Probe on multiplexer_2_out
  Multiplexer #(.Bits(4)) multiplexer_3 (.sel(MDR[5]), .in_0(MDR[3:0]), .in_1(IMM[7:4]), .out(multiplexer_3_out));
  nor nor_1 (nor_1_out, IMM[4], IMM[5], IMM[6], IMM[7]);
  Register #(.Bits(8)) u_PC (.D(multiplexer_2_out), .C(clk_t), .en(PC_plus_1), .Q(PC));
  // Probe on multiplexer_3_out
  Register #(.Bits(4)) u_MAR (.D(multiplexer_3_out), .C(clk_t), .en(1'b1), .Q(MAR));
  Multiplexer multiplexer_4 (.sel(model), .in_0(hand), .in_1(clock), .out(multiplexer_4_out));
  Add #(.Bits(8)) add_1 (.a(8'h1), .b(PC), .c_i(1'b0), .s(add_1_s));  // open: c_o
  // Probe on MAR
  ROM #(.AddrBits(4), .Bits(16), .Addr_Bits(6)) MROM (
    .A(MAR), .sel(1'b1), .D({ALUop, LDPC, MDR[11:8], Asel, MDR[5:0]}));
  and and_2 (hlt, MDR[5], nor_1_out, I_0);
  or or_1 (clk_t, multiplexer_4_out, break_q);
  // Probe on PC
  ROM #(.AddrBits(8), .Bits(8)) ROM (.A(PC), .sel(1'b1), .D({IMM, I_0}));
  // Probe on PC
  // Probe on {ALUop, LDPC, MDR[11:8], Asel, MDR[5:0]}
  // Probe on MDR[3:0]
  and and_3 (and_3_out, reset, multiplexer_4_out);
  // Probe on {IMM, I_0}
  // Probe on IMM[7:4]
  Register #(.Bits(4)) register_1 (.D({IMM[3:1], I_0}), .C(clk_t), .en(MDR[5]), .Q({Ra, Rb}));
  D_FF_AS \break  (.Set(1'b0), .D(hlt), .C(clk_t), .Clr(and_3_out), .Q(break_q));  // open: nQ
  Seven_Seg_Hex seven_seg_hex_1 (.d(counter_1_out), .dp(1'b0));
  Counter #(.Bits(4)) counter_1 (.en(1'b1), .C(MDR[5]), .clr(1'b0), .out(counter_1_out));  // open: ovf
  nand nand_1 (nand_1_out, I_10, MDR[4]);
  // Probe on Rb
  // Probe on Ra
  LED led_1 (.in(break_q));
  and and_4 (PC_plus_1, nand_1_out, MDR[8]);
  or or_2 (I_10, Rb[0], Rb[1]);
  and and_5 (and_5_out, memw, ~Yin[7]);  // And
  Multiplexer #(.Bits(8)) multiplexer_5 (.sel(I_10), .in_0({IMM, I_0}), .in_1(Db), .out(Yin));
  // Bus bus_1: pin names not known; wires that end beside it: clk, {ALUop, LDPC, MDR[11:8], Asel, MDR[5:0], IMM, I_0, MAR, PC[3:0]}, {bus_1_p3, in}
  // Probe on Rin
  // Probe on Min
  RAMDualPort #(.AddrBits(7), .Bits(8)) Dram (
    .A(Yin[6:0]), .Din(Min), .str(and_5_out), .C(clk_t), .ld(1'b1), .D(Dram_d));
  ROM #(.AddrBits(7), .Bits(8)) Drom (.A(Yin[6:0]), .sel(1'b1), .D(Drom_d));
  Register #(.Bits(8)) register_2 (.D(out_t), .C(clk_t), .en(ENout), .Q(OUT));
  // Probe on in
  RegisterFile #(.Bits(8)) regs (.Din(Rin), .we(regw), .Rw(Ra), .C(clk_t), .Ra(Ra), .Rb(Rb), .Da(Da), .Db(Db));
  Multiplexer #(.Bits(8)) multiplexer_6 (.sel(Yin[7]), .in_0(Dram_d), .in_1(Drom_d), .out(Mout));
  // Probe on Da
  // Probe on Db
  // Probe on Mout
  LED led_2 (.in(OUT[7]));
  // Probe on Yin
  Add #(.Bits(8)) add_2 (.a(Xin), .b(Yin), .c_i(1'b0), .s(add_2_s), .c_o(C_F));
  Sub #(.Bits(8)) sub_1 (.a(Xin), .b(Yin), .c_i(1'b0), .s(sub_1_s));  // open: c_o
  Mul #(.Bits(8)) mul_1 (.a(Xin), .b(Yin), .mul({mul_1_mul_2, mul_1_mul}));
  assign and_6_out = Xin & Yin;  // And and_6, 8 bits wide
  assign or_3_out = Xin | Yin;  // Or or_3, 8 bits wide
  assign xor_1_out = Xin ^ Yin;  // XOr xor_1, 8 bits wide
  Multiplexer #(.Selector_Bits(3), .Bits(8)) multiplexer_7 (
    .sel(MDR[11:9]), .in_0({8{1'b0}}), .in_1(Da), .in_2(Mout), .in_3(in), .in_4({IMM, I_0}), .in_5(Db),
    .in_6({8{1'b0}}), .in_7({8{1'b0}}), .out(Xin));
  // Probe on MDR[11:9]
  // Probe on Xin
  // Probe on ALUop
  Multiplexer #(.Selector_Bits(3), .Bits(8)) multiplexer_8 (
    .sel(ALUop), .in_0(Xin), .in_1(add_2_s), .in_2(sub_1_s), .in_3(mul_1_mul), .in_4(and_6_out),
    .in_5(or_3_out), .in_6(xor_1_out), .in_7(multiplexer_9_out), .out({S_F, multiplexer_8_out}));
  BarrelShifter #(.Bits(8)) barrelshifter_1 (.in(Xin), .shift({IMM[3:1], I_0}), .out(barrelshifter_1_out));
  BarrelShifter #(.Bits(8), .direction("right")) barrelshifter_2 (
    .in(Xin), .shift({IMM[3:1], I_0}), .out(barrelshifter_2_out));
  BarrelShifter #(.Bits(8), .barrelShifterMode("rotate")) barrelshifter_3 (
    .in(Xin), .shift({IMM[3:1], I_0}), .out(barrelshifter_3_out));
  BarrelShifter #(.Bits(8), .barrelShifterMode("rotate"), .direction("right")) barrelshifter_4 (
    .in(Xin), .shift({IMM[3:1], I_0}), .out(barrelshifter_4_out));
  // Probe on {IMM[3:1], I_0}
  Comparator #(.Bits(8)) comparator_1 (.a({S_F, multiplexer_8_out}), .b({8{1'b0}}), .eq(Z_F));  // open: gt, lt
  Decoder #(.Selector_Bits(2)) decoder_1 (.sel(Asel), .out_1(regw), .out_2(memw), .out_3(ENout));  // open: out_0
  Demultiplexer #(.Selector_Bits(2), .Bits(8)) demultiplexer_1 (
    .sel(Asel), .in({S_F, multiplexer_8_out}), .out_1(Rin), .out_2(Min), .out_3(out_t));  // open: out_0
  // Probe on Asel
  Multiplexer #(.Selector_Bits(2), .Bits(8)) multiplexer_9 (
    .sel(Rb), .in_0(barrelshifter_1_out), .in_1(barrelshifter_2_out), .in_2(barrelshifter_3_out),
    .in_3(barrelshifter_4_out), .out(multiplexer_9_out));
  // Probe on Rb

  // Other names for the same wires on the sheet: IMM[0] = I_0; OP[3:0] = IMM[7:4]; P2 = MDR[4]; P1 = MDR[5];
  //   MDR (some bits) = {ALUop, LDPC, Asel}; PC_INC = MDR[8]; Ssel[2:0] = MDR[11:9]

  // Notes on the sheet:
  //   clk: Hz: 10
  //   clock: Hz: 2
  //   微程序控制器
  //   contents of MROM (hex, n*v repeats v):
  //   120,1100,a40,940,640,2c0,550,390,0,2350,4350,6350,8350,a350,c350,e340
  //   contents of ROM (hex, n*v repeats v):
  //   30,4,34,3,4c,5c,74,3,28,72,60,3,66,1
  //   存储器
  //   寄存器
  //   Drom loads instruction_monocycle.hex
  //   数据通路+运算器
endmodule
