// Digital circuit ARMv8 pipe-2.dig as structural Verilog
module ARMv8_pipe_2 (
  input  clock,
  input  hand,
  input  model,
  input  reset,
  input  [63:0] IN,
  output [7:0] IOaddr,
  output [63:0] OUT
);

  wire and_1_out, and_2_out, and_3_out, and_4_out, and_5_out, and_6_out, and_7_out, and_9_out, and_11_out,
       and_12_out, and_13_out, and_14_out, and_15_out, and_16_out, and_17_out, and_18_out, and_20_out,
       break_q, brk, C, C_plus, C_t, clk, comparator_1_eq, comparator_2_eq, comparator_3_eq, Dsel, IO_EN,
       memw, multiplexer_4_out, multiplexer_5_out, N1, N2, nor_1_out, nor_2_out, nor_3_out, nor_4_out,
       not_1_out, or_2_out, or_3_out, or_7_out, regw, V, xor_1_out, xor_2_out, Z, zero;
  wire [1:0] hw, pcsel, size;
  wire [1:1] shift;
  wire [2:0] cond;
  wire [3:0] aluop, vncz;
  wire [4:0] imm16, rs1addr_ID, rs2addr_ID, rwaddr_EX;
  wire [5:0] imm6_s;
  wire [6:0] multiplexer_11_out;
  wire [8:4] imm9;
  wire [18:5] Irom_d_2;
  wire [19:0] pc_q;
  wire [25:0] bitextender_1_out, Irom_d, multiplexer_1_out, multiplexer_2_out;
  wire [29:0] IR_ID_EX_q;
  wire [31:26] Irom_d_3;
  wire [62:0] multiplexer_15_out, rs1;
  wire [63:0] add_1_s, add_2_s, ALU_EX, and_19_out, ASR_out, bitextender_2_out, bitextender_3_out,
       bitextender_4_out, Dram_d, Drom_d, LSL_MOV_out, LSL_out, LSR_out, multiplexer_3_out,
       multiplexer_8_out, multiplexer_12_out, multiplexer_13_out, multiplexer_14_out, multiplexer_16_out,
       multiplexer_17_out, multiplexer_18_out, multiplexer_19_out, multiplexer_20_out, or_6_out, PC_ID_EX_q,
       plus_2_s, plus_s, ROR_out, rs1_ID, rs2, rs2_ID, rs_jump, rw_EX, sub_s, xor_3_out;
  wire [63:20] pc_q_2;

  BitExtender #(.inputBits(19), .outputBits(26)) bitextender_1 (.in({Irom_d_2, rs1addr_ID}), .out(bitextender_1_out));
  Multiplexer #(.Bits(26)) multiplexer_1 (
    .sel(multiplexer_5_out), .in_0(26'h1), .in_1(bitextender_1_out), .out(multiplexer_1_out));
  Multiplexer #(.Selector_Bits(2), .Bits(26)) multiplexer_2 (
    .sel(pcsel), .in_0(26'h1), .in_1({Irom_d[25:24], Irom_d_2, rs1addr_ID, Irom_d[4], cond, Irom_d[0]}),
    .in_2(multiplexer_1_out), .in_3({26{1'b0}}), .out(multiplexer_2_out));
  Multiplexer #(.Selector_Bits(2), .Bits(64)) multiplexer_3 (
    .sel(pcsel), .in_0({pc_q_2, pc_q}), .in_1({pc_q_2, pc_q}), .in_2({pc_q_2, pc_q}), .in_3({N1, rs1}),
    .out(multiplexer_3_out));
  BitExtender #(.inputBits(26), .outputBits(64)) bitextender_2 (.in(multiplexer_2_out), .out(bitextender_2_out));
  and and_1 (and_1_out, vncz[0], vncz[3]);
  nor nor_1 (nor_1_out, vncz[2], and_1_out);
  and and_2 (and_2_out, reset, multiplexer_4_out);
  // Probe on pcsel
  Comparator comparator_1 (.a(vncz[3]), .b(vncz[2]), .eq(comparator_1_eq));  // open: gt, lt
  Multiplexer multiplexer_4 (.sel(model), .in_0(hand), .in_1(clock), .out(multiplexer_4_out));
  Add #(.Bits(64)) add_1 (.a(multiplexer_3_out), .b(bitextender_2_out), .c_i(1'b0), .s(add_1_s));  // open: c_o
  D_FF_AS \break  (.Set(1'b0), .D(brk), .C(clk), .Clr(and_2_out), .Q(break_q));  // open: nQ
  or or_1 (clk, break_q, multiplexer_4_out);
  // Probe on add_1_s
  Register #(.Bits(64)) pc (.D(add_1_s), .C(clk), .en(1'b1), .Q({pc_q_2, pc_q}));
  and and_3 (and_3_out, ~vncz[0], vncz[1]);  // And
  LED led_1 (.in(break_q));
  ROM #(.AddrBits(20), .Bits(32)) Irom (
    .A(pc_q), .sel(1'b1), .D({Irom_d_3, Irom_d[25:24], Irom_d_2, rs1addr_ID, Irom_d[4], cond, Irom_d[0]}));
  Multiplexer #(.Selector_Bits(3)) multiplexer_5 (
    .sel(cond), .in_0(vncz[0]), .in_1(vncz[1]), .in_2(vncz[2]), .in_3(vncz[3]), .in_4(and_3_out),
    .in_5(comparator_1_eq), .in_6(nor_1_out), .in_7(1'b0), .out(multiplexer_5_out));
  // Probe on cond
  // Probe on rs1addr_ID
  Comparator #(.Bits(5)) comparator_2 (.a(rs1addr_ID), .b(rwaddr_EX), .eq(comparator_2_eq));  // open: gt, lt
  // Probe on rs2addr_ID
  Comparator #(.Bits(5)) comparator_3 (.a(rs2addr_ID), .b(rwaddr_EX), .eq(comparator_3_eq));  // open: gt, lt
  // Probe on rwaddr_EX
  // pcsel pcsel_1: pin names not known; wires that end beside it: Irom_d_3[31], Irom_d_3[30], Irom_d_3[29], Irom_d_3[28], Irom_d_3[27], Irom_d_3[26], Irom_d[25], pcsel[1], pcsel[0]
  and and_4 (and_4_out, regw, comparator_2_eq);
  and and_5 (and_5_out, regw, comparator_3_eq);
  Multiplexer #(.Bits(5)) multiplexer_6 (
    .sel(and_7_out), .in_0(Irom_d_2[15:11]), .in_1({Irom_d[4], cond, Irom_d[0]}), .out(rs2addr_ID));
  and and_6 (and_6_out, Irom_d_3[29], Irom_d_3[28], Irom_d_3[27]);
  nor nor_2 (nor_2_out, Irom_d_3[26], Irom_d[25], Irom_d[24], Irom_d_2[18], Irom_d_2[17], Irom_d_2[16]);
  // Probe on rw_EX
  // Probe on rwaddr_EX
  // Probe PC_ID on {pc_q_2, pc_q}
  // Probe on rs1_ID
  Multiplexer #(.Bits(64)) multiplexer_7 (.sel(and_4_out), .in_0(rs1_ID), .in_1(rw_EX), .out(rs_jump));
  // Probe on rw_EX
  // Probe on rs2_ID
  Multiplexer #(.Bits(64)) multiplexer_8 (.sel(and_5_out), .in_0(rs2_ID), .in_1(rw_EX), .out(multiplexer_8_out));
  // Probe on rw_EX
  and and_7 (and_7_out, and_6_out, nor_2_out);
  RegisterFile #(.AddrBits(5), .Bits(64)) regs (
    .Din(rw_EX), .we(regw), .Rw(rwaddr_EX), .C(clk), .Ra(rs1addr_ID), .Rb(rs2addr_ID), .Da(rs1_ID),
    .Db(rs2_ID));
  // Probe on rs_jump
  // Probe on multiplexer_8_out
  D_FF memw_ID_EX (.D(and_7_out), .C(clk), .Q(memw));  // open: nQ
  // Probe on rs1_ID
  // Probe on rs2_ID
  // Probe IR_ID on {Irom_d_3, Irom_d[25:24], Irom_d_2, rs1addr_ID, Irom_d[4], cond, Irom_d[0]}
  Register #(.Bits(32)) IR_ID_EX (
    .D({Irom_d_3, Irom_d[25:24], Irom_d_2, rs1addr_ID, Irom_d[4], cond, Irom_d[0]}), .C(clk), .en(1'b1),
    .Q({size, IR_ID_EX_q[29:24], shift[1], hw, imm9, imm6_s, imm16, IR_ID_EX_q[4:0]}));
  Register #(.Bits(64)) PC_ID_EX (.D({pc_q_2, pc_q}), .C(clk), .en(1'b1), .Q(PC_ID_EX_q));
  Register #(.Bits(64)) rs1_ID_EX (.D(rs_jump), .C(clk), .en(1'b1), .Q({N1, rs1}));
  Register #(.Bits(64)) rs2_ID_EX (.D(multiplexer_8_out), .C(clk), .en(1'b1), .Q(rs2));
  // Probe IR_EX on {size, IR_ID_EX_q[29:24], shift[1], hw, imm9, imm6_s, imm16, IR_ID_EX_q[4:0]}
  // Probe PC_EX on PC_ID_EX_q
  // Probe on {N1, rs1}
  // Probe on rs2
  aluop_III aluop_iii_1 (
    ._30(size[0]), ._29(IR_ID_EX_q[29]), ._28(IR_ID_EX_q[28]), ._27(IR_ID_EX_q[27]), ._26(IR_ID_EX_q[26]),
    ._25(IR_ID_EX_q[25]), ._24(IR_ID_EX_q[24]), ._23(shift[1]), ._3(aluop[3]), ._2(aluop[2]), ._1(aluop[1]),
    ._0(aluop[0]));
  Add #(.Bits(64)) add_2 (.a(PC_ID_EX_q), .b(64'h1), .c_i(1'b0), .s(add_2_s));  // open: c_o
  Comparator #(.Bits(5)) comparator_4 (.a(IR_ID_EX_q[4:0]), .b({5{1'b1}}), .eq(zero));  // open: gt, lt
  nor nor_3 (nor_3_out, IR_ID_EX_q[29], IR_ID_EX_q[27], IR_ID_EX_q[25], IR_ID_EX_q[24]);
  or or_2 (or_2_out, aluop[3], aluop[2], aluop[1], aluop[0]);
  // Dsel dsel_1: pin names not known; wires that end beside it: size[1], size[0], IR_ID_EX_q[29], IR_ID_EX_q[28], IR_ID_EX_q[27], IR_ID_EX_q[26], IR_ID_EX_q[25], hw[0], Dsel
  Multiplexer #(.Bits(64)) multiplexer_9 (.sel(Dsel), .in_0(ALU_EX), .in_1(add_2_s), .out(rw_EX));
  Multiplexer #(.Bits(5)) multiplexer_10 (.sel(Dsel), .in_0(IR_ID_EX_q[4:0]), .in_1(5'b11110), .out(rwaddr_EX));
  and and_8 (brk, size[1], size[0], IR_ID_EX_q[28], IR_ID_EX_q[26], nor_3_out);
  and and_9 (and_9_out, ~memw, or_2_out);  // And
  or or_3 (or_3_out, and_9_out, Dsel);
  and and_10 (regw, or_3_out, ~zero);  // And
  // Probe on Dsel
  xor xor_1 (xor_1_out, N1, N2);
  Multiplexer #(.Bits(7)) multiplexer_11 (
    .sel(aluop[3]), .in_0({1'b0, imm6_s}), .in_1({7{1'b0}}), .out(multiplexer_11_out));
  Comparator #(.Bits(12)) comparator_5 (.a(plus_s[19:8]), .b({12{1'b1}}), .eq(IO_EN));  // open: gt, lt
  BitExtender #(.inputBits(9), .outputBits(64)) bitextender_3 (.in({imm9, imm6_s[5:2]}), .out(bitextender_3_out));
  and and_11 (and_11_out, IO_EN, memw);
  xor xor_2 (xor_2_out, ALU_EX[63], N1);
  not not_1 (not_1_out, xor_1_out);
  and and_12 (and_12_out, aluop[3], ~aluop[2], ~aluop[1]);  // And
  and and_13 (and_13_out, aluop[3], ~aluop[2], aluop[1]);  // And
  BarrelShifter #(.Bits(64)) LSL (.in(rs2), .shift({1'b0, imm6_s}), .out(LSL_out));
  BarrelShifter #(.Bits(64), .direction("right")) LSR (.in(rs2), .shift({1'b0, imm6_s}), .out(LSR_out));
  BarrelShifter #(.Bits(64), .barrelShifterMode("arithmetic"), .direction("right")) ASR (
    .in(rs2), .shift({1'b0, imm6_s}), .out(ASR_out));
  BarrelShifter #(.Bits(64), .barrelShifterMode("rotate"), .direction("right")) ROR (
    .in(rs2), .shift(multiplexer_11_out), .out(ROR_out));
  Add #(.Bits(64)) plus (.a({N1, rs1}), .b(bitextender_3_out), .c_i(1'b0), .s(plus_s));  // open: c_o
  Register #(.Bits(64)) register_1 (.D(rs2), .C(clk), .en(and_11_out), .Q(OUT));
  BitExtender #(.inputBits(13), .outputBits(64)) bitextender_4 (.in({hw, imm9, imm6_s}), .out(bitextender_4_out));
  Register #(.Bits(8)) register_2 (.D(plus_s[7:0]), .C(~clk), .en(IO_EN), .Q(IOaddr));
  // Probe on plus_s
  and and_14 (and_14_out, xor_2_out, not_1_out, and_12_out);
  and and_15 (and_15_out, xor_2_out, xor_1_out, and_13_out);
  and and_16 (and_16_out, and_12_out, C_plus);
  and and_17 (and_17_out, and_13_out, C_t);
  Multiplexer #(.Selector_Bits(2), .Bits(64)) multiplexer_12 (
    .sel({shift[1], hw[1]}), .in_0(LSL_out), .in_1(LSR_out), .in_2(ASR_out), .in_3(ROR_out),
    .out(multiplexer_12_out));
  Multiplexer #(.Bits(64)) multiplexer_13 (
    .sel(hw[1]), .in_0({{52{1'b0}}, hw[0], imm9, imm6_s}),
    .in_1({{40{1'b0}}, hw[0], imm9, imm6_s, {12{1'b0}}}), .out(multiplexer_13_out));
  and and_18 (and_18_out, plus_s[20], ~IO_EN, memw);  // And
  or or_4 (V, and_14_out, and_15_out);
  or or_5 (C, and_16_out, and_17_out);
  BarrelShifter #(.Bits(64)) LSL_MOV (
    .in({{48{1'b0}}, imm9, imm6_s, imm16}), .shift({1'b0, hw, 4'b0000}), .out(LSL_MOV_out));
  Multiplexer #(.Bits(64)) multiplexer_14 (
    .sel(aluop[0]), .in_0(multiplexer_12_out), .in_1(bitextender_4_out), .out(multiplexer_14_out));
  Multiplexer #(.Bits(64)) multiplexer_15 (
    .sel(aluop[0]), .in_0(multiplexer_12_out), .in_1(multiplexer_13_out), .out({N2, multiplexer_15_out}));
  assign and_19_out = {N1, rs1} & multiplexer_14_out;  // And and_19, 64 bits wide
  assign or_6_out = {N1, rs1} | multiplexer_14_out;  // Or or_6, 64 bits wide
  assign xor_3_out = {N1, rs1} ^ multiplexer_14_out;  // XOr xor_3, 64 bits wide
  ROM #(.AddrBits(20), .Bits(64)) Drom (.A(plus_s[19:0]), .sel(1'b1), .D(Drom_d));
  RAMDualPort #(.AddrBits(20), .Bits(64)) Dram (
    .A(plus_s[19:0]), .Din(rs2), .str(and_18_out), .C(clk), .ld(1'b1), .D(Dram_d));
  Multiplexer #(.Bits(64)) multiplexer_16 (
    .sel(aluop[0]), .in_0({64{1'b0}}), .in_1(LSL_MOV_out), .out(multiplexer_16_out));
  Add #(.Bits(64)) plus_2 (.a({N1, rs1}), .b({N2, multiplexer_15_out}), .c_i(1'b0), .s(plus_2_s), .c_o(C_plus));
  Sub #(.Bits(64)) sub (.a({N1, rs1}), .b({N2, multiplexer_15_out}), .c_i(1'b0), .s(sub_s), .c_o(C_t));
  Multiplexer #(.Bits(64)) multiplexer_17 (.sel(plus_s[20]), .in_0(Drom_d), .in_1(Dram_d), .out(multiplexer_17_out));
  nor nor_4 (nor_4_out, aluop[3], aluop[2], ~aluop[1]);  // NOr
  Multiplexer #(.Selector_Bits(2), .Bits(64)) multiplexer_18 (
    .sel(aluop[2:1]), .in_0(multiplexer_16_out), .in_1(and_19_out), .in_2(or_6_out), .in_3(xor_3_out),
    .out(multiplexer_18_out));
  Multiplexer #(.Selector_Bits(2), .Bits(64)) multiplexer_19 (
    .sel(aluop[2:1]), .in_0(plus_2_s), .in_1(sub_s), .in_2(multiplexer_20_out), .in_3({64{1'b0}}),
    .out(multiplexer_19_out));
  Multiplexer #(.Bits(64)) multiplexer_20 (.sel(IO_EN), .in_0(multiplexer_17_out), .in_1(IN), .out(multiplexer_20_out));
  and and_20 (and_20_out, aluop[3], ~aluop[2]);  // And
  Multiplexer #(.Bits(64)) multiplexer_21 (
    .sel(aluop[3]), .in_0(multiplexer_18_out), .in_1(multiplexer_19_out), .out(ALU_EX));
  // Probe on aluop[2:1]
  Register #(.Bits(4)) u_VNCZ (.D({V, ALU_EX[63], C, Z}), .C(~clk), .en(or_7_out), .Q(vncz));
  or or_7 (or_7_out, and_20_out, nor_4_out);
  // Probe on ALU_EX
  Comparator #(.Bits(64)) comparator_6 (.a({64{1'b0}}), .b(ALU_EX), .eq(Z));  // open: gt, lt

  // Other names for the same wires on the sheet: imm12[11:0] = {hw[0], imm9, imm6_s}; imm16[15:5] = {imm9, imm6_s};
  //   imm9[3:0] = imm6_s[5:2]; immr[5:0] = {hw[0], imm9}; sh_N = hw[1]; shift[0] = hw[1]; N = ALU_EX[63];
  //   rs1[63] = N1

  // Notes on the sheet:
  //   clock: Hz: 2
  //   PC
  //   B
  //   B.cond
  //   BR
  //   Redirect
  //   contents of Irom (hex, n*v repeats v):
  //   d2800021,d2a00202,f8400020,f8001040,b1000421,b1000442,f100143f,54000040,97fffffa,
  //   d4200000
  //   controller EX
  //   ALU
  //   MEM
  //   contents of Drom (hex, n*v repeats v):
  //   8,aa,ff,80,55
endmodule
