// Digital circuit ARMv8 CPU-I.dig as structural Verilog
module ARMv8_CPU_I (
  input  clock,
  input  hand,
  input  model,
  input  reset,
  input  [3:0] VNCZ
);

  wire and_1_out, and_2_out, and_4_out, break_q, brk, clk, comparator_1_eq, Dsel, multiplexer_4_out,
       multiplexer_6_out, nor_1_out, nor_2_out, regw, zero;
  wire [1:0] pcsel;
  wire [2:0] cond;
  wire [4:0] multiplexer_5_out;
  wire [18:0] Irom_d_2;
  wire [19:0] pc_q;
  wire [25:0] bitextender_1_out, Irom_d, multiplexer_1_out, multiplexer_2_out;
  wire [31:26] dsel_1_p6;
  wire [63:0] add_1_s, add_2_s, bitextender_2_out, multiplexer_3_out, rs1;
  wire [63:20] pc_q_2;

  // Probe on {Irom_d[25:24], Irom_d_2, Irom_d[4], cond, Irom_d[0]}
  BitExtender #(.inputBits(19), .outputBits(26)) bitextender_1 (.in(Irom_d_2), .out(bitextender_1_out));
  Multiplexer #(.Bits(26)) multiplexer_1 (
    .sel(multiplexer_4_out), .in_0(26'h1), .in_1(bitextender_1_out), .out(multiplexer_1_out));
  // Probe on bitextender_1_out
  and and_1 (and_1_out, VNCZ[0], VNCZ[3]);
  nor nor_1 (nor_1_out, VNCZ[2], and_1_out);
  Multiplexer #(.Selector_Bits(2), .Bits(26)) multiplexer_2 (
    .sel(pcsel), .in_0(26'h1), .in_1({Irom_d[25:24], Irom_d_2, Irom_d[4], cond, Irom_d[0]}),
    .in_2(multiplexer_1_out), .in_3({26{1'b0}}), .out(multiplexer_2_out));
  BitExtender #(.inputBits(26), .outputBits(64)) bitextender_2 (.in(multiplexer_2_out), .out(bitextender_2_out));
  Comparator comparator_1 (.a(VNCZ[3]), .b(VNCZ[2]), .eq(comparator_1_eq));  // open: gt, lt
  Multiplexer #(.Selector_Bits(2), .Bits(64)) multiplexer_3 (
    .sel(pcsel), .in_0({pc_q_2, pc_q}), .in_1({pc_q_2, pc_q}), .in_2({pc_q_2, pc_q}), .in_3(rs1),
    .out(multiplexer_3_out));
  Add #(.Bits(64)) add_1 (.a(multiplexer_3_out), .b(bitextender_2_out), .c_i(1'b0), .s(add_1_s));  // open: c_o
  // Probe on pcsel
  and and_2 (and_2_out, ~VNCZ[0], VNCZ[1]);  // And
  // Probe on add_1_s
  Register #(.Bits(64)) pc (.D(add_1_s), .C(clk), .en(1'b1), .Q({pc_q_2, pc_q}));
  Multiplexer #(.Selector_Bits(3)) multiplexer_4 (
    .sel(cond), .in_0(VNCZ[0]), .in_1(VNCZ[1]), .in_2(VNCZ[2]), .in_3(VNCZ[3]), .in_4(and_2_out),
    .in_5(comparator_1_eq), .in_6(nor_1_out), .in_7(1'b0), .out(multiplexer_4_out));
  // Probe on cond
  // Probe on {pc_q_2, pc_q}
  Add #(.Bits(64)) add_2 (.a({pc_q_2, pc_q}), .b(64'h1), .c_i(1'b0), .s(add_2_s));  // open: c_o
  // Dsel dsel_1: pin names not known; wires that end beside it: dsel_1_p6[31], dsel_1_p6[30], dsel_1_p6[29], dsel_1_p6[28], dsel_1_p6[27], dsel_1_p6[26], Irom_d[25], Irom_d_2[16], Dsel
  // pcsel pcsel_1: pin names not known; wires that end beside it: dsel_1_p6[31], dsel_1_p6[30], dsel_1_p6[29], dsel_1_p6[28], dsel_1_p6[27], dsel_1_p6[26], Irom_d[25], pcsel[1], pcsel[0]
  // Probe on pc_q
  ROM #(.AddrBits(20), .Bits(32)) Irom (
    .A(pc_q), .sel(1'b1), .D({dsel_1_p6, Irom_d[25:24], Irom_d_2, Irom_d[4], cond, Irom_d[0]}));
  // Probe on {dsel_1_p6, Irom_d[25:24], Irom_d_2, Irom_d[4], cond, Irom_d[0]}
  and and_3 (regw, ~zero, Dsel);  // And
  Multiplexer #(.Bits(5)) multiplexer_5 (
    .sel(Dsel), .in_0({Irom_d[4], cond, Irom_d[0]}), .in_1(5'b11110), .out(multiplexer_5_out));
  and and_4 (and_4_out, reset, multiplexer_6_out);
  Multiplexer multiplexer_6 (.sel(model), .in_0(hand), .in_1(clock), .out(multiplexer_6_out));
  Comparator #(.Bits(5)) comparator_2 (.a({Irom_d[4], cond, Irom_d[0]}), .b({5{1'b1}}), .eq(zero));  // open: gt, lt
  or or_1 (clk, break_q, multiplexer_6_out);
  and and_5 (brk, dsel_1_p6[31], dsel_1_p6[30], dsel_1_p6[28], dsel_1_p6[26], nor_2_out);
  nor nor_2 (nor_2_out, dsel_1_p6[29], dsel_1_p6[27], Irom_d[25], Irom_d[24]);
  RegisterFile #(.AddrBits(5), .Bits(64)) regs (
    .Din(add_2_s), .we(regw), .Rw(multiplexer_5_out), .C(clk), .Ra(Irom_d_2[4:0]), .Rb(Irom_d_2[15:11]),
    .Da(rs1));  // open: Db
  D_FF_AS \break  (.Set(1'b0), .D(brk), .C(clk), .Clr(and_4_out), .Q(break_q));  // open: nQ
  // Probe on rs1
  LED led_1 (.in(break_q));

  // Notes on the sheet:
  //   clock: Hz: 2
  //   PC
  //   B
  //   B.cond
  //   BR
  //   controller I
  //   contents of Irom (hex, n*v repeats v):
  //   14000007,d4200000,94000002,d503201f,d503201f,d61f03c0,d4200000,54ffff64,d4200000
endmodule
