// Digital circuit ARMv8 CPU-III - 副本.dig as structural Verilog
module \ARMv8_CPU_III___副本  (
  input  clock,
  input  hand,
  input  model,
  input  reset,
  input  [63:0] IN,
  output [7:0] IOaddr,
  output [63:0] OUT
);

  wire and_1_out, and_2_out, and_3_out, and_4_out, and_6_out, and_7_out, and_8_out, and_9_out, and_10_out,
       and_11_out, and_12_out, and_13_out, and_14_out, and_17_out, break_q, brk, C, C_plus, C_t, clk,
       comparator_2_eq, Dsel, IO_EN, memw, multiplexer_15_out, multiplexer_19_out, N, N1, N2, nor_1_out,
       nor_2_out, nor_3_out, nor_4_out, not_1_out, or_1_out, or_6_out, or_7_out, regw, V, xor_2_out,
       xor_3_out, Z, zero;
  wire [1:0] hw, pcsel, size;
  wire [1:1] shift;
  wire [2:0] cond;
  wire [3:0] aluop, VNCZ_q;
  wire [4:0] imm16, multiplexer_17_out, multiplexer_18_out;
  wire [5:0] imm6_s;
  wire [6:0] multiplexer_1_out;
  wire [7:0] plus_s;
  wire [8:4] imm9;
  wire [11:0] plus_s_2;
  wire [19:0] pc_q;
  wire [25:0] bitextender_1_out, Irom_d, multiplexer_2_out, multiplexer_3_out;
  wire [29:26] Irom_d_2;
  wire [62:0] multiplexer_8_out, multiplexer_13_out, rs1;
  wire [63:0] add_1_s, add_2_s, and_5_out, ASR_out, bitextender_2_out, bitextender_3_out, bitextender_4_out,
       Dram_d, Drom_d, LSL_MOV_out, LSL_out, LSR_out, multiplexer_4_out, multiplexer_5_out,
       multiplexer_6_out, multiplexer_7_out, multiplexer_9_out, multiplexer_10_out, multiplexer_11_out,
       multiplexer_12_out, multiplexer_14_out, multiplexer_16_out, or_2_out, plus_2_s, ROR_out, rs2, sub_s,
       xor_1_out;
  wire [63:20] pc_q_2, plus_s_3;

  BitExtender #(.inputBits(19), .outputBits(26)) bitextender_1 (
    .in({shift[1], hw, imm9, imm6_s, imm16}), .out(bitextender_1_out));
  Multiplexer #(.Bits(7)) multiplexer_1 (
    .sel(aluop[3]), .in_0({1'b0, imm6_s}), .in_1({7{1'b0}}), .out(multiplexer_1_out));
  Comparator #(.Bits(12)) comparator_1 (.a(plus_s_2), .b({12{1'b1}}), .eq(IO_EN));  // open: gt, lt
  BitExtender #(.inputBits(9), .outputBits(64)) bitextender_2 (.in({imm9, imm6_s[5:2]}), .out(bitextender_2_out));
  and and_1 (and_1_out, IO_EN, memw);
  // Probe on {V, N, C, Z}
  Register #(.Bits(4)) VNCZ (.D({V, N, C, Z}), .C(clk), .en(or_1_out), .Q(VNCZ_q));
  and and_2 (and_2_out, aluop[3], ~aluop[2]);  // And
  nor nor_1 (nor_1_out, aluop[3], aluop[2], ~aluop[1]);  // NOr
  Add #(.Bits(64)) plus (
    .a({N1, rs1}), .b(bitextender_2_out), .c_i(1'b0), .s({plus_s_3, plus_s_2, plus_s}));  // open: c_o
  Register #(.Bits(64)) register_1 (.D(rs2), .C(clk), .en(and_1_out), .Q(OUT));
  Multiplexer #(.Bits(26)) multiplexer_2 (
    .sel(multiplexer_15_out), .in_0(26'h1), .in_1(bitextender_1_out), .out(multiplexer_2_out));
  or or_1 (or_1_out, and_2_out, nor_1_out);
  BarrelShifter #(.Bits(64)) LSL (.in(rs2), .shift({1'b0, imm6_s}), .out(LSL_out));
  BarrelShifter #(.Bits(64), .direction("right")) LSR (.in(rs2), .shift({1'b0, imm6_s}), .out(LSR_out));
  BarrelShifter #(.Bits(64), .barrelShifterMode("arithmetic"), .direction("right")) ASR (
    .in(rs2), .shift({1'b0, imm6_s}), .out(ASR_out));
  BarrelShifter #(.Bits(64), .barrelShifterMode("rotate"), .direction("right")) ROR (
    .in(rs2), .shift(multiplexer_1_out), .out(ROR_out));
  Register #(.Bits(8)) register_2 (.D(plus_s), .C(~clk), .en(IO_EN), .Q(IOaddr));
  // Probe on {plus_s_3, plus_s_2, plus_s}
  Multiplexer #(.Selector_Bits(2), .Bits(26)) multiplexer_3 (
    .sel(pcsel), .in_0(26'h1),
    .in_1({Irom_d[25:24], shift[1], hw, imm9, imm6_s, imm16, Irom_d[4], cond, Irom_d[0]}),
    .in_2(multiplexer_2_out), .in_3({26{1'b0}}), .out(multiplexer_3_out));
  Multiplexer #(.Selector_Bits(2), .Bits(64)) multiplexer_4 (
    .sel({shift[1], hw[1]}), .in_0(LSL_out), .in_1(LSR_out), .in_2(ASR_out), .in_3(ROR_out),
    .out(multiplexer_4_out));
  BitExtender #(.inputBits(13), .outputBits(64)) bitextender_3 (.in({hw, imm9, imm6_s}), .out(bitextender_3_out));
  Multiplexer #(.Bits(64)) multiplexer_5 (
    .sel(hw[1]), .in_0({{52{1'b0}}, hw[0], imm9, imm6_s}),
    .in_1({{40{1'b0}}, hw[0], imm9, imm6_s, {12{1'b0}}}), .out(multiplexer_5_out));
  and and_3 (and_3_out, plus_s_3[20], ~IO_EN, memw);  // And
  Multiplexer #(.Selector_Bits(2), .Bits(64)) multiplexer_6 (
    .sel(pcsel), .in_0({pc_q_2, pc_q}), .in_1({pc_q_2, pc_q}), .in_2({pc_q_2, pc_q}), .in_3({N1, rs1}),
    .out(multiplexer_6_out));
  BitExtender #(.inputBits(26), .outputBits(64)) bitextender_4 (.in(multiplexer_3_out), .out(bitextender_4_out));
  and and_4 (and_4_out, VNCZ_q[0], VNCZ_q[3]);
  nor nor_2 (nor_2_out, VNCZ_q[2], and_4_out);
  BarrelShifter #(.Bits(64)) LSL_MOV (
    .in({{48{1'b0}}, imm9, imm6_s, imm16}), .shift({1'b0, hw, 4'b0000}), .out(LSL_MOV_out));
  Multiplexer #(.Bits(64)) multiplexer_7 (
    .sel(aluop[0]), .in_0(multiplexer_4_out), .in_1(bitextender_3_out), .out(multiplexer_7_out));
  Multiplexer #(.Bits(64)) multiplexer_8 (
    .sel(aluop[0]), .in_0(multiplexer_4_out), .in_1(multiplexer_5_out), .out({N2, multiplexer_8_out}));
  // Probe on pcsel
  Comparator comparator_2 (.a(VNCZ_q[3]), .b(VNCZ_q[2]), .eq(comparator_2_eq));  // open: gt, lt
  assign and_5_out = {N1, rs1} & multiplexer_7_out;  // And and_5, 64 bits wide
  assign or_2_out = {N1, rs1} | multiplexer_7_out;  // Or or_2, 64 bits wide
  assign xor_1_out = {N1, rs1} ^ multiplexer_7_out;  // XOr xor_1, 64 bits wide
  ROM #(.AddrBits(20), .Bits(64)) Drom (.A({plus_s_2, plus_s}), .sel(1'b1), .D(Drom_d));
  RAMDualPort #(.AddrBits(20), .Bits(64)) Dram (
    .A({plus_s_2, plus_s}), .Din(rs2), .str(and_3_out), .C(clk), .ld(1'b1), .D(Dram_d));
  Add #(.Bits(64)) add_1 (.a(multiplexer_6_out), .b(bitextender_4_out), .c_i(1'b0), .s(add_1_s));  // open: c_o
  Multiplexer #(.Bits(64)) multiplexer_9 (
    .sel(aluop[0]), .in_0({64{1'b0}}), .in_1(LSL_MOV_out), .out(multiplexer_9_out));
  Add #(.Bits(64)) plus_2 (.a({N1, rs1}), .b({N2, multiplexer_8_out}), .c_i(1'b0), .s(plus_2_s), .c_o(C_plus));
  Sub #(.Bits(64)) sub (.a({N1, rs1}), .b({N2, multiplexer_8_out}), .c_i(1'b0), .s(sub_s), .c_o(C_t));
  Multiplexer #(.Bits(64)) multiplexer_10 (.sel(plus_s_3[20]), .in_0(Drom_d), .in_1(Dram_d), .out(multiplexer_10_out));
  // Probe on add_1_s
  Register #(.Bits(64)) pc (.D(add_1_s), .C(clk), .en(1'b1), .Q({pc_q_2, pc_q}));
  and and_6 (and_6_out, ~VNCZ_q[0], VNCZ_q[1]);  // And
  Multiplexer #(.Selector_Bits(2), .Bits(64)) multiplexer_11 (
    .sel(aluop[2:1]), .in_0(multiplexer_9_out), .in_1(and_5_out), .in_2(or_2_out), .in_3(xor_1_out),
    .out(multiplexer_11_out));
  Multiplexer #(.Bits(64)) multiplexer_12 (.sel(IO_EN), .in_0(multiplexer_10_out), .in_1(IN), .out(multiplexer_12_out));
  // Probe on {pc_q_2, pc_q}
  Multiplexer #(.Bits(64)) multiplexer_13 (
    .sel(aluop[3]), .in_0(multiplexer_11_out), .in_1(multiplexer_14_out), .out({N, multiplexer_13_out}));
  Multiplexer #(.Selector_Bits(2), .Bits(64)) multiplexer_14 (
    .sel(aluop[2:1]), .in_0(plus_2_s), .in_1(sub_s), .in_2(multiplexer_12_out), .in_3({64{1'b0}}),
    .out(multiplexer_14_out));
  // Probe on aluop[2:1]
  Add #(.Bits(64)) add_2 (.a({pc_q_2, pc_q}), .b(64'h1), .c_i(1'b0), .s(add_2_s));  // open: c_o
  ROM #(.AddrBits(20), .Bits(32)) Irom (
    .A(pc_q), .sel(1'b1),
    .D({size, Irom_d_2, Irom_d[25:24], shift[1], hw, imm9, imm6_s, imm16, Irom_d[4], cond, Irom_d[0]}));
  Multiplexer #(.Selector_Bits(3)) multiplexer_15 (
    .sel(cond), .in_0(VNCZ_q[0]), .in_1(VNCZ_q[1]), .in_2(VNCZ_q[2]), .in_3(VNCZ_q[3]), .in_4(and_6_out),
    .in_5(comparator_2_eq), .in_6(nor_2_out), .in_7(1'b0), .out(multiplexer_15_out));
  // Probe on {N, multiplexer_13_out}
  Comparator #(.Bits(64)) comparator_3 (.a({64{1'b0}}), .b({N, multiplexer_13_out}), .eq(Z));  // open: gt, lt
  xor xor_2 (xor_2_out, N1, N2);
  Multiplexer #(.Bits(64)) multiplexer_16 (
    .sel(Dsel), .in_0({N, multiplexer_13_out}), .in_1(add_2_s), .out(multiplexer_16_out));
  xor xor_3 (xor_3_out, N, N1);
  and and_7 (and_7_out, aluop[3], ~aluop[2], ~aluop[1]);  // And
  and and_8 (and_8_out, aluop[3], ~aluop[2], aluop[1]);  // And
  and and_9 (and_9_out, reset, multiplexer_19_out);
  not not_1 (not_1_out, xor_2_out);
  Multiplexer #(.Bits(5)) multiplexer_17 (
    .sel(Dsel), .in_0({Irom_d[4], cond, Irom_d[0]}), .in_1(5'b11110), .out(multiplexer_17_out));
  Multiplexer #(.Bits(5)) multiplexer_18 (
    .sel(memw), .in_0(imm9), .in_1({Irom_d[4], cond, Irom_d[0]}), .out(multiplexer_18_out));
  // Probe on {size, Irom_d_2, Irom_d[25:24], shift[1], hw, imm9, imm6_s, imm16, Irom_d[4], cond, Irom_d[0]}
  Multiplexer multiplexer_19 (.sel(model), .in_0(hand), .in_1(clock), .out(multiplexer_19_out));
  and and_10 (and_10_out, xor_3_out, not_1_out, and_7_out);
  and and_11 (and_11_out, xor_3_out, xor_2_out, and_8_out);
  and and_12 (and_12_out, and_7_out, C_plus);
  and and_13 (and_13_out, and_8_out, C_t);
  RegisterFile #(.AddrBits(5), .Bits(64)) regs (
    .Din(multiplexer_16_out), .we(regw), .Rw(multiplexer_17_out), .C(clk), .Ra(imm16),
    .Rb(multiplexer_18_out), .Da({N1, rs1}), .Db(rs2));
  D_FF_AS \break  (.Set(1'b0), .D(brk), .C(clk), .Clr(and_9_out), .Q(break_q));  // open: nQ
  or or_3 (clk, break_q, multiplexer_19_out);
  or or_4 (V, and_10_out, and_11_out);
  or or_5 (C, and_12_out, and_13_out);
  LED led_1 (.in(break_q));
  // Probe on {N1, rs1}
  // Probe on rs2
  aluop_III aluop_iii_1 (
    ._30(size[0]), ._29(Irom_d_2[29]), ._28(Irom_d_2[28]), ._27(Irom_d_2[27]), ._26(Irom_d_2[26]),
    ._25(Irom_d[25]), ._24(Irom_d[24]), ._23(shift[1]), ._3(aluop[3]), ._2(aluop[2]), ._1(aluop[1]),
    ._0(aluop[0]));
  Comparator #(.Bits(5)) comparator_4 (.a({Irom_d[4], cond, Irom_d[0]}), .b({5{1'b1}}), .eq(zero));  // open: gt, lt
  and and_14 (and_14_out, Irom_d_2[29], Irom_d_2[28], Irom_d_2[27]);
  nor nor_3 (nor_3_out, Irom_d_2[26], Irom_d[25], Irom_d[24], shift[1], hw[1], hw[0]);
  nor nor_4 (nor_4_out, Irom_d_2[29], Irom_d_2[27], Irom_d[25], Irom_d[24]);
  or or_6 (or_6_out, aluop[3], aluop[2], aluop[1], aluop[0]);
  // Dsel dsel_1: pin names not known; wires that end beside it: size[1], size[0], Irom_d_2[29], Irom_d_2[28], Irom_d_2[27], Irom_d_2[26], Irom_d[25], hw[0], Dsel
  // pcsel pcsel_1: pin names not known; wires that end beside it: size[1], size[0], Irom_d_2[29], Irom_d_2[28], Irom_d_2[27], Irom_d_2[26], Irom_d[25], pcsel[1], pcsel[0]
  and and_15 (memw, and_14_out, nor_3_out);
  and and_16 (brk, size[1], size[0], Irom_d_2[28], Irom_d_2[26], nor_4_out);
  and and_17 (and_17_out, ~memw, or_6_out);  // And
  or or_7 (or_7_out, and_17_out, Dsel);
  and and_18 (regw, or_7_out, ~zero);  // And

  // Other names for the same wires on the sheet: imm12[11:0] = {hw[0], imm9, imm6_s}; imm16[15:5] = {imm9, imm6_s};
  //   imm9[3:0] = imm6_s[5:2]; immr[5:0] = {hw[0], imm9}; sh_N = hw[1]; shift[0] = hw[1]; rs1[63] = N1

  // Notes on the sheet:
  //   clock: Hz: 2
  //   PC
  //   ALU
  //   MEM
  //   B
  //   B.cond
  //   BR
  //   contents of Drom (hex, n*v repeats v):
  //   8,aa,ff,80,55
  //   contents of Irom (hex, n*v repeats v):
  //   d2800021,d2a00202,f8400020,f8001040,b1000421,d100143f,f100143f,54000040,97fffffa,
  //   d4200000
  //   controller III
endmodule
